// Logisim project demo.circ as structural Verilog: 1 circuit, main circuit main
module main (
  input  Left_Right
);

  wire Clock_out;
  wire [10:0] counter_1_q;
  wire [15:0] rom_1_data, rom_2_data, rom_3_data, rom_4_data, rom_5_data, rom_6_data, rom_7_data, rom_8_data,
       rom_9_data, rom_10_data, rom_11_data, rom_12_data, rom_13_data, rom_14_data, rom_15_data, rom_16_data,
       rom_17_data, rom_18_data, rom_19_data, rom_20_data, rom_21_data, rom_22_data, rom_23_data,
       rom_24_data, rom_25_data, rom_26_data, rom_27_data, rom_28_data, rom_29_data, rom_30_data,
       rom_31_data, rom_32_data, rom_33_data, rom_34_data, rom_35_data, rom_36_data, rom_37_data,
       rom_38_data, rom_39_data, rom_40_data, rom_41_data, rom_42_data, rom_43_data, rom_44_data,
       rom_45_data, rom_46_data, rom_47_data, rom_48_data, rom_49_data, rom_50_data, rom_51_data,
       rom_52_data, rom_53_data, rom_54_data, rom_55_data, rom_56_data, rom_57_data, rom_58_data,
       rom_59_data, rom_60_data, rom_61_data, rom_62_data, rom_63_data, rom_64_data, rom_65_data,
       rom_66_data, rom_67_data, rom_68_data, rom_69_data, rom_70_data, rom_71_data, rom_72_data,
       rom_73_data, rom_74_data, rom_75_data, rom_76_data, rom_77_data, rom_78_data, rom_79_data,
       rom_80_data, rom_81_data, rom_82_data, rom_83_data, rom_84_data, rom_85_data, rom_86_data,
       rom_87_data, rom_88_data, rom_89_data, rom_90_data, rom_91_data, rom_92_data, rom_93_data,
       rom_94_data, rom_95_data, rom_96_data, rom_97_data, rom_98_data, rom_99_data, rom_100_data,
       rom_101_data, rom_102_data, rom_103_data, rom_104_data, rom_105_data, rom_106_data, rom_107_data,
       rom_108_data, rom_109_data, rom_110_data, rom_111_data, rom_112_data, rom_113_data, rom_114_data,
       rom_115_data, rom_116_data, rom_117_data, rom_118_data, rom_119_data, rom_120_data, rom_121_data,
       rom_122_data, rom_123_data, rom_124_data, rom_125_data, rom_126_data, rom_127_data, rom_128_data,
       rom_129_data, rom_130_data, rom_131_data, rom_132_data, rom_133_data, rom_134_data, rom_135_data,
       rom_136_data, rom_137_data, rom_138_data, rom_139_data, rom_140_data, rom_141_data, rom_142_data,
       rom_143_data, rom_144_data, rom_145_data, rom_146_data, rom_147_data, rom_148_data, rom_149_data,
       rom_150_data, rom_151_data, rom_152_data, rom_153_data, rom_154_data, rom_155_data, rom_156_data,
       rom_157_data, rom_158_data, rom_159_data, rom_160_data;

  Counter #(.width(11), .max('h66f)) counter_1 (
    .load(Left_Right), .Q(counter_1_q), .clk(Clock_out));  // open: D, count, carry, clr
  Clock Clock (.out(Clock_out));
  DotMatrix #(.matrixcols(16), .matrixrows(16)) dotmatrix_1 (
    .col0(rom_1_data), .col1(rom_2_data), .col2(rom_3_data), .col3(rom_4_data), .col4(rom_5_data),
    .col5(rom_6_data), .col6(rom_7_data), .col7(rom_8_data), .col8(rom_9_data), .col9(rom_10_data),
    .col10(rom_11_data), .col11(rom_12_data), .col12(rom_13_data), .col13(rom_14_data), .col14(rom_15_data),
    .col15(rom_16_data));
  ROM #(.addrWidth(11), .dataWidth(16)) rom_1 (.addr(counter_1_q), .data(rom_1_data));  // open: sel
  ROM #(.addrWidth(11), .dataWidth(16)) rom_2 (.addr(counter_1_q), .data(rom_2_data));  // open: sel
  ROM #(.addrWidth(11), .dataWidth(16)) rom_3 (.addr(counter_1_q), .data(rom_3_data));  // open: sel
  ROM #(.addrWidth(11), .dataWidth(16)) rom_4 (.addr(counter_1_q), .data(rom_4_data));  // open: sel
  ROM #(.addrWidth(11), .dataWidth(16)) rom_5 (.addr(counter_1_q), .data(rom_5_data));  // open: sel
  ROM #(.addrWidth(11), .dataWidth(16)) rom_6 (.addr(counter_1_q), .data(rom_6_data));  // open: sel
  ROM #(.addrWidth(11), .dataWidth(16)) rom_7 (.addr(counter_1_q), .data(rom_7_data));  // open: sel
  ROM #(.addrWidth(11), .dataWidth(16)) rom_8 (.addr(counter_1_q), .data(rom_8_data));  // open: sel
  ROM #(.addrWidth(11), .dataWidth(16)) rom_9 (.addr(counter_1_q), .data(rom_9_data));  // open: sel
  ROM #(.addrWidth(11), .dataWidth(16)) rom_10 (.addr(counter_1_q), .data(rom_10_data));  // open: sel
  ROM #(.addrWidth(11), .dataWidth(16)) rom_11 (.addr(counter_1_q), .data(rom_11_data));  // open: sel
  ROM #(.addrWidth(11), .dataWidth(16)) rom_12 (.addr(counter_1_q), .data(rom_12_data));  // open: sel
  ROM #(.addrWidth(11), .dataWidth(16)) rom_13 (.addr(counter_1_q), .data(rom_13_data));  // open: sel
  ROM #(.addrWidth(11), .dataWidth(16)) rom_14 (.addr(counter_1_q), .data(rom_14_data));  // open: sel
  ROM #(.addrWidth(11), .dataWidth(16)) rom_15 (.addr(counter_1_q), .data(rom_15_data));  // open: sel
  ROM #(.addrWidth(11), .dataWidth(16)) rom_16 (.addr(counter_1_q), .data(rom_16_data));  // open: sel
  ROM #(.addrWidth(11), .dataWidth(16)) rom_17 (.addr(counter_1_q), .data(rom_17_data));  // open: sel
  ROM #(.addrWidth(11), .dataWidth(16)) rom_18 (.addr(counter_1_q), .data(rom_18_data));  // open: sel
  ROM #(.addrWidth(11), .dataWidth(16)) rom_19 (.addr(counter_1_q), .data(rom_19_data));  // open: sel
  ROM #(.addrWidth(11), .dataWidth(16)) rom_20 (.addr(counter_1_q), .data(rom_20_data));  // open: sel
  ROM #(.addrWidth(11), .dataWidth(16)) rom_21 (.addr(counter_1_q), .data(rom_21_data));  // open: sel
  ROM #(.addrWidth(11), .dataWidth(16)) rom_22 (.addr(counter_1_q), .data(rom_22_data));  // open: sel
  ROM #(.addrWidth(11), .dataWidth(16)) rom_23 (.addr(counter_1_q), .data(rom_23_data));  // open: sel
  ROM #(.addrWidth(11), .dataWidth(16)) rom_24 (.addr(counter_1_q), .data(rom_24_data));  // open: sel
  ROM #(.addrWidth(11), .dataWidth(16)) rom_25 (.addr(counter_1_q), .data(rom_25_data));  // open: sel
  ROM #(.addrWidth(11), .dataWidth(16)) rom_26 (.addr(counter_1_q), .data(rom_26_data));  // open: sel
  ROM #(.addrWidth(11), .dataWidth(16)) rom_27 (.addr(counter_1_q), .data(rom_27_data));  // open: sel
  ROM #(.addrWidth(11), .dataWidth(16)) rom_28 (.addr(counter_1_q), .data(rom_28_data));  // open: sel
  ROM #(.addrWidth(11), .dataWidth(16)) rom_29 (.addr(counter_1_q), .data(rom_29_data));  // open: sel
  ROM #(.addrWidth(11), .dataWidth(16)) rom_30 (.addr(counter_1_q), .data(rom_30_data));  // open: sel
  ROM #(.addrWidth(11), .dataWidth(16)) rom_31 (.addr(counter_1_q), .data(rom_31_data));  // open: sel
  ROM #(.addrWidth(11), .dataWidth(16)) rom_32 (.addr(counter_1_q), .data(rom_32_data));  // open: sel
  ROM #(.addrWidth(11), .dataWidth(16)) rom_33 (.addr(counter_1_q), .data(rom_33_data));  // open: sel
  ROM #(.addrWidth(11), .dataWidth(16)) rom_34 (.addr(counter_1_q), .data(rom_34_data));  // open: sel
  ROM #(.addrWidth(11), .dataWidth(16)) rom_35 (.addr(counter_1_q), .data(rom_35_data));  // open: sel
  ROM #(.addrWidth(11), .dataWidth(16)) rom_36 (.addr(counter_1_q), .data(rom_36_data));  // open: sel
  ROM #(.addrWidth(11), .dataWidth(16)) rom_37 (.addr(counter_1_q), .data(rom_37_data));  // open: sel
  ROM #(.addrWidth(11), .dataWidth(16)) rom_38 (.addr(counter_1_q), .data(rom_38_data));  // open: sel
  ROM #(.addrWidth(11), .dataWidth(16)) rom_39 (.addr(counter_1_q), .data(rom_39_data));  // open: sel
  ROM #(.addrWidth(11), .dataWidth(16)) rom_40 (.addr(counter_1_q), .data(rom_40_data));  // open: sel
  ROM #(.addrWidth(11), .dataWidth(16)) rom_41 (.addr(counter_1_q), .data(rom_41_data));  // open: sel
  ROM #(.addrWidth(11), .dataWidth(16)) rom_42 (.addr(counter_1_q), .data(rom_42_data));  // open: sel
  ROM #(.addrWidth(11), .dataWidth(16)) rom_43 (.addr(counter_1_q), .data(rom_43_data));  // open: sel
  ROM #(.addrWidth(11), .dataWidth(16)) rom_44 (.addr(counter_1_q), .data(rom_44_data));  // open: sel
  ROM #(.addrWidth(11), .dataWidth(16)) rom_45 (.addr(counter_1_q), .data(rom_45_data));  // open: sel
  ROM #(.addrWidth(11), .dataWidth(16)) rom_46 (.addr(counter_1_q), .data(rom_46_data));  // open: sel
  ROM #(.addrWidth(11), .dataWidth(16)) rom_47 (.addr(counter_1_q), .data(rom_47_data));  // open: sel
  ROM #(.addrWidth(11), .dataWidth(16)) rom_48 (.addr(counter_1_q), .data(rom_48_data));  // open: sel
  ROM #(.addrWidth(11), .dataWidth(16)) rom_49 (.addr(counter_1_q), .data(rom_49_data));  // open: sel
  ROM #(.addrWidth(11), .dataWidth(16)) rom_50 (.addr(counter_1_q), .data(rom_50_data));  // open: sel
  ROM #(.addrWidth(11), .dataWidth(16)) rom_51 (.addr(counter_1_q), .data(rom_51_data));  // open: sel
  ROM #(.addrWidth(11), .dataWidth(16)) rom_52 (.addr(counter_1_q), .data(rom_52_data));  // open: sel
  ROM #(.addrWidth(11), .dataWidth(16)) rom_53 (.addr(counter_1_q), .data(rom_53_data));  // open: sel
  ROM #(.addrWidth(11), .dataWidth(16)) rom_54 (.addr(counter_1_q), .data(rom_54_data));  // open: sel
  ROM #(.addrWidth(11), .dataWidth(16)) rom_55 (.addr(counter_1_q), .data(rom_55_data));  // open: sel
  ROM #(.addrWidth(11), .dataWidth(16)) rom_56 (.addr(counter_1_q), .data(rom_56_data));  // open: sel
  ROM #(.addrWidth(11), .dataWidth(16)) rom_57 (.addr(counter_1_q), .data(rom_57_data));  // open: sel
  ROM #(.addrWidth(11), .dataWidth(16)) rom_58 (.addr(counter_1_q), .data(rom_58_data));  // open: sel
  ROM #(.addrWidth(11), .dataWidth(16)) rom_59 (.addr(counter_1_q), .data(rom_59_data));  // open: sel
  ROM #(.addrWidth(11), .dataWidth(16)) rom_60 (.addr(counter_1_q), .data(rom_60_data));  // open: sel
  ROM #(.addrWidth(11), .dataWidth(16)) rom_61 (.addr(counter_1_q), .data(rom_61_data));  // open: sel
  ROM #(.addrWidth(11), .dataWidth(16)) rom_62 (.addr(counter_1_q), .data(rom_62_data));  // open: sel
  ROM #(.addrWidth(11), .dataWidth(16)) rom_63 (.addr(counter_1_q), .data(rom_63_data));  // open: sel
  ROM #(.addrWidth(11), .dataWidth(16)) rom_64 (.addr(counter_1_q), .data(rom_64_data));  // open: sel
  ROM #(.addrWidth(11), .dataWidth(16)) rom_65 (.addr(counter_1_q), .data(rom_65_data));  // open: sel
  ROM #(.addrWidth(11), .dataWidth(16)) rom_66 (.addr(counter_1_q), .data(rom_66_data));  // open: sel
  ROM #(.addrWidth(11), .dataWidth(16)) rom_67 (.addr(counter_1_q), .data(rom_67_data));  // open: sel
  ROM #(.addrWidth(11), .dataWidth(16)) rom_68 (.addr(counter_1_q), .data(rom_68_data));  // open: sel
  ROM #(.addrWidth(11), .dataWidth(16)) rom_69 (.addr(counter_1_q), .data(rom_69_data));  // open: sel
  ROM #(.addrWidth(11), .dataWidth(16)) rom_70 (.addr(counter_1_q), .data(rom_70_data));  // open: sel
  ROM #(.addrWidth(11), .dataWidth(16)) rom_71 (.addr(counter_1_q), .data(rom_71_data));  // open: sel
  ROM #(.addrWidth(11), .dataWidth(16)) rom_72 (.addr(counter_1_q), .data(rom_72_data));  // open: sel
  ROM #(.addrWidth(11), .dataWidth(16)) rom_73 (.addr(counter_1_q), .data(rom_73_data));  // open: sel
  ROM #(.addrWidth(11), .dataWidth(16)) rom_74 (.addr(counter_1_q), .data(rom_74_data));  // open: sel
  ROM #(.addrWidth(11), .dataWidth(16)) rom_75 (.addr(counter_1_q), .data(rom_75_data));  // open: sel
  ROM #(.addrWidth(11), .dataWidth(16)) rom_76 (.addr(counter_1_q), .data(rom_76_data));  // open: sel
  ROM #(.addrWidth(11), .dataWidth(16)) rom_77 (.addr(counter_1_q), .data(rom_77_data));  // open: sel
  ROM #(.addrWidth(11), .dataWidth(16)) rom_78 (.addr(counter_1_q), .data(rom_78_data));  // open: sel
  ROM #(.addrWidth(11), .dataWidth(16)) rom_79 (.addr(counter_1_q), .data(rom_79_data));  // open: sel
  ROM #(.addrWidth(11), .dataWidth(16)) rom_80 (.addr(counter_1_q), .data(rom_80_data));  // open: sel
  ROM #(.addrWidth(11), .dataWidth(16)) rom_81 (.addr(counter_1_q), .data(rom_81_data));  // open: sel
  ROM #(.addrWidth(11), .dataWidth(16)) rom_82 (.addr(counter_1_q), .data(rom_82_data));  // open: sel
  ROM #(.addrWidth(11), .dataWidth(16)) rom_83 (.addr(counter_1_q), .data(rom_83_data));  // open: sel
  ROM #(.addrWidth(11), .dataWidth(16)) rom_84 (.addr(counter_1_q), .data(rom_84_data));  // open: sel
  ROM #(.addrWidth(11), .dataWidth(16)) rom_85 (.addr(counter_1_q), .data(rom_85_data));  // open: sel
  ROM #(.addrWidth(11), .dataWidth(16)) rom_86 (.addr(counter_1_q), .data(rom_86_data));  // open: sel
  ROM #(.addrWidth(11), .dataWidth(16)) rom_87 (.addr(counter_1_q), .data(rom_87_data));  // open: sel
  ROM #(.addrWidth(11), .dataWidth(16)) rom_88 (.addr(counter_1_q), .data(rom_88_data));  // open: sel
  ROM #(.addrWidth(11), .dataWidth(16)) rom_89 (.addr(counter_1_q), .data(rom_89_data));  // open: sel
  ROM #(.addrWidth(11), .dataWidth(16)) rom_90 (.addr(counter_1_q), .data(rom_90_data));  // open: sel
  ROM #(.addrWidth(11), .dataWidth(16)) rom_91 (.addr(counter_1_q), .data(rom_91_data));  // open: sel
  ROM #(.addrWidth(11), .dataWidth(16)) rom_92 (.addr(counter_1_q), .data(rom_92_data));  // open: sel
  ROM #(.addrWidth(11), .dataWidth(16)) rom_93 (.addr(counter_1_q), .data(rom_93_data));  // open: sel
  ROM #(.addrWidth(11), .dataWidth(16)) rom_94 (.addr(counter_1_q), .data(rom_94_data));  // open: sel
  ROM #(.addrWidth(11), .dataWidth(16)) rom_95 (.addr(counter_1_q), .data(rom_95_data));  // open: sel
  ROM #(.addrWidth(11), .dataWidth(16)) rom_96 (.addr(counter_1_q), .data(rom_96_data));  // open: sel
  ROM #(.addrWidth(11), .dataWidth(16)) rom_97 (.addr(counter_1_q), .data(rom_97_data));  // open: sel
  ROM #(.addrWidth(11), .dataWidth(16)) rom_98 (.addr(counter_1_q), .data(rom_98_data));  // open: sel
  ROM #(.addrWidth(11), .dataWidth(16)) rom_99 (.addr(counter_1_q), .data(rom_99_data));  // open: sel
  ROM #(.addrWidth(11), .dataWidth(16)) rom_100 (.addr(counter_1_q), .data(rom_100_data));  // open: sel
  ROM #(.addrWidth(11), .dataWidth(16)) rom_101 (.addr(counter_1_q), .data(rom_101_data));  // open: sel
  ROM #(.addrWidth(11), .dataWidth(16)) rom_102 (.addr(counter_1_q), .data(rom_102_data));  // open: sel
  ROM #(.addrWidth(11), .dataWidth(16)) rom_103 (.addr(counter_1_q), .data(rom_103_data));  // open: sel
  ROM #(.addrWidth(11), .dataWidth(16)) rom_104 (.addr(counter_1_q), .data(rom_104_data));  // open: sel
  ROM #(.addrWidth(11), .dataWidth(16)) rom_105 (.addr(counter_1_q), .data(rom_105_data));  // open: sel
  ROM #(.addrWidth(11), .dataWidth(16)) rom_106 (.addr(counter_1_q), .data(rom_106_data));  // open: sel
  ROM #(.addrWidth(11), .dataWidth(16)) rom_107 (.addr(counter_1_q), .data(rom_107_data));  // open: sel
  ROM #(.addrWidth(11), .dataWidth(16)) rom_108 (.addr(counter_1_q), .data(rom_108_data));  // open: sel
  ROM #(.addrWidth(11), .dataWidth(16)) rom_109 (.addr(counter_1_q), .data(rom_109_data));  // open: sel
  ROM #(.addrWidth(11), .dataWidth(16)) rom_110 (.addr(counter_1_q), .data(rom_110_data));  // open: sel
  ROM #(.addrWidth(11), .dataWidth(16)) rom_111 (.addr(counter_1_q), .data(rom_111_data));  // open: sel
  ROM #(.addrWidth(11), .dataWidth(16)) rom_112 (.addr(counter_1_q), .data(rom_112_data));  // open: sel
  ROM #(.addrWidth(11), .dataWidth(16)) rom_113 (.addr(counter_1_q), .data(rom_113_data));  // open: sel
  ROM #(.addrWidth(11), .dataWidth(16)) rom_114 (.addr(counter_1_q), .data(rom_114_data));  // open: sel
  ROM #(.addrWidth(11), .dataWidth(16)) rom_115 (.addr(counter_1_q), .data(rom_115_data));  // open: sel
  ROM #(.addrWidth(11), .dataWidth(16)) rom_116 (.addr(counter_1_q), .data(rom_116_data));  // open: sel
  ROM #(.addrWidth(11), .dataWidth(16)) rom_117 (.addr(counter_1_q), .data(rom_117_data));  // open: sel
  ROM #(.addrWidth(11), .dataWidth(16)) rom_118 (.addr(counter_1_q), .data(rom_118_data));  // open: sel
  ROM #(.addrWidth(11), .dataWidth(16)) rom_119 (.addr(counter_1_q), .data(rom_119_data));  // open: sel
  ROM #(.addrWidth(11), .dataWidth(16)) rom_120 (.addr(counter_1_q), .data(rom_120_data));  // open: sel
  ROM #(.addrWidth(11), .dataWidth(16)) rom_121 (.addr(counter_1_q), .data(rom_121_data));  // open: sel
  ROM #(.addrWidth(11), .dataWidth(16)) rom_122 (.addr(counter_1_q), .data(rom_122_data));  // open: sel
  ROM #(.addrWidth(11), .dataWidth(16)) rom_123 (.addr(counter_1_q), .data(rom_123_data));  // open: sel
  ROM #(.addrWidth(11), .dataWidth(16)) rom_124 (.addr(counter_1_q), .data(rom_124_data));  // open: sel
  ROM #(.addrWidth(11), .dataWidth(16)) rom_125 (.addr(counter_1_q), .data(rom_125_data));  // open: sel
  ROM #(.addrWidth(11), .dataWidth(16)) rom_126 (.addr(counter_1_q), .data(rom_126_data));  // open: sel
  ROM #(.addrWidth(11), .dataWidth(16)) rom_127 (.addr(counter_1_q), .data(rom_127_data));  // open: sel
  ROM #(.addrWidth(11), .dataWidth(16)) rom_128 (.addr(counter_1_q), .data(rom_128_data));  // open: sel
  ROM #(.addrWidth(11), .dataWidth(16)) rom_129 (.addr(counter_1_q), .data(rom_129_data));  // open: sel
  ROM #(.addrWidth(11), .dataWidth(16)) rom_130 (.addr(counter_1_q), .data(rom_130_data));  // open: sel
  ROM #(.addrWidth(11), .dataWidth(16)) rom_131 (.addr(counter_1_q), .data(rom_131_data));  // open: sel
  ROM #(.addrWidth(11), .dataWidth(16)) rom_132 (.addr(counter_1_q), .data(rom_132_data));  // open: sel
  ROM #(.addrWidth(11), .dataWidth(16)) rom_133 (.addr(counter_1_q), .data(rom_133_data));  // open: sel
  ROM #(.addrWidth(11), .dataWidth(16)) rom_134 (.addr(counter_1_q), .data(rom_134_data));  // open: sel
  ROM #(.addrWidth(11), .dataWidth(16)) rom_135 (.addr(counter_1_q), .data(rom_135_data));  // open: sel
  ROM #(.addrWidth(11), .dataWidth(16)) rom_136 (.addr(counter_1_q), .data(rom_136_data));  // open: sel
  ROM #(.addrWidth(11), .dataWidth(16)) rom_137 (.addr(counter_1_q), .data(rom_137_data));  // open: sel
  ROM #(.addrWidth(11), .dataWidth(16)) rom_138 (.addr(counter_1_q), .data(rom_138_data));  // open: sel
  ROM #(.addrWidth(11), .dataWidth(16)) rom_139 (.addr(counter_1_q), .data(rom_139_data));  // open: sel
  ROM #(.addrWidth(11), .dataWidth(16)) rom_140 (.addr(counter_1_q), .data(rom_140_data));  // open: sel
  ROM #(.addrWidth(11), .dataWidth(16)) rom_141 (.addr(counter_1_q), .data(rom_141_data));  // open: sel
  ROM #(.addrWidth(11), .dataWidth(16)) rom_142 (.addr(counter_1_q), .data(rom_142_data));  // open: sel
  ROM #(.addrWidth(11), .dataWidth(16)) rom_143 (.addr(counter_1_q), .data(rom_143_data));  // open: sel
  ROM #(.addrWidth(11), .dataWidth(16)) rom_144 (.addr(counter_1_q), .data(rom_144_data));  // open: sel
  ROM #(.addrWidth(11), .dataWidth(16)) rom_145 (.addr(counter_1_q), .data(rom_145_data));  // open: sel
  ROM #(.addrWidth(11), .dataWidth(16)) rom_146 (.addr(counter_1_q), .data(rom_146_data));  // open: sel
  ROM #(.addrWidth(11), .dataWidth(16)) rom_147 (.addr(counter_1_q), .data(rom_147_data));  // open: sel
  ROM #(.addrWidth(11), .dataWidth(16)) rom_148 (.addr(counter_1_q), .data(rom_148_data));  // open: sel
  ROM #(.addrWidth(11), .dataWidth(16)) rom_149 (.addr(counter_1_q), .data(rom_149_data));  // open: sel
  ROM #(.addrWidth(11), .dataWidth(16)) rom_150 (.addr(counter_1_q), .data(rom_150_data));  // open: sel
  ROM #(.addrWidth(11), .dataWidth(16)) rom_151 (.addr(counter_1_q), .data(rom_151_data));  // open: sel
  ROM #(.addrWidth(11), .dataWidth(16)) rom_152 (.addr(counter_1_q), .data(rom_152_data));  // open: sel
  ROM #(.addrWidth(11), .dataWidth(16)) rom_153 (.addr(counter_1_q), .data(rom_153_data));  // open: sel
  ROM #(.addrWidth(11), .dataWidth(16)) rom_154 (.addr(counter_1_q), .data(rom_154_data));  // open: sel
  ROM #(.addrWidth(11), .dataWidth(16)) rom_155 (.addr(counter_1_q), .data(rom_155_data));  // open: sel
  ROM #(.addrWidth(11), .dataWidth(16)) rom_156 (.addr(counter_1_q), .data(rom_156_data));  // open: sel
  ROM #(.addrWidth(11), .dataWidth(16)) rom_157 (.addr(counter_1_q), .data(rom_157_data));  // open: sel
  ROM #(.addrWidth(11), .dataWidth(16)) rom_158 (.addr(counter_1_q), .data(rom_158_data));  // open: sel
  ROM #(.addrWidth(11), .dataWidth(16)) rom_159 (.addr(counter_1_q), .data(rom_159_data));  // open: sel
  ROM #(.addrWidth(11), .dataWidth(16)) rom_160 (.addr(counter_1_q), .data(rom_160_data));  // open: sel
  DotMatrix #(.matrixcols(16), .matrixrows(16)) dotmatrix_2 (
    .col0(rom_17_data), .col1(rom_18_data), .col2(rom_19_data), .col3(rom_20_data), .col4(rom_21_data),
    .col5(rom_22_data), .col6(rom_23_data), .col7(rom_24_data), .col8(rom_25_data), .col9(rom_26_data),
    .col10(rom_27_data), .col11(rom_28_data), .col12(rom_29_data), .col13(rom_30_data), .col14(rom_31_data),
    .col15(rom_32_data));
  DotMatrix #(.matrixcols(16), .matrixrows(16)) dotmatrix_3 (
    .col0(rom_33_data), .col1(rom_34_data), .col2(rom_35_data), .col3(rom_36_data), .col4(rom_37_data),
    .col5(rom_38_data), .col6(rom_39_data), .col7(rom_40_data), .col8(rom_41_data), .col9(rom_42_data),
    .col10(rom_43_data), .col11(rom_44_data), .col12(rom_45_data), .col13(rom_46_data), .col14(rom_47_data),
    .col15(rom_48_data));
  DotMatrix #(.matrixcols(16), .matrixrows(16)) dotmatrix_4 (
    .col0(rom_49_data), .col1(rom_50_data), .col2(rom_51_data), .col3(rom_52_data), .col4(rom_53_data),
    .col5(rom_54_data), .col6(rom_55_data), .col7(rom_56_data), .col8(rom_57_data), .col9(rom_58_data),
    .col10(rom_59_data), .col11(rom_60_data), .col12(rom_61_data), .col13(rom_62_data), .col14(rom_63_data),
    .col15(rom_64_data));
  DotMatrix #(.matrixcols(16), .matrixrows(16)) dotmatrix_5 (
    .col0(rom_65_data), .col1(rom_66_data), .col2(rom_67_data), .col3(rom_68_data), .col4(rom_69_data),
    .col5(rom_70_data), .col6(rom_71_data), .col7(rom_72_data), .col8(rom_73_data), .col9(rom_74_data),
    .col10(rom_75_data), .col11(rom_76_data), .col12(rom_77_data), .col13(rom_78_data), .col14(rom_79_data),
    .col15(rom_80_data));
  DotMatrix #(.matrixcols(16), .matrixrows(16)) dotmatrix_6 (
    .col0(rom_81_data), .col1(rom_82_data), .col2(rom_83_data), .col3(rom_84_data), .col4(rom_85_data),
    .col5(rom_86_data), .col6(rom_87_data), .col7(rom_88_data), .col8(rom_89_data), .col9(rom_90_data),
    .col10(rom_91_data), .col11(rom_92_data), .col12(rom_93_data), .col13(rom_94_data), .col14(rom_95_data),
    .col15(rom_96_data));
  DotMatrix #(.matrixcols(16), .matrixrows(16)) dotmatrix_7 (
    .col0(rom_97_data), .col1(rom_98_data), .col2(rom_99_data), .col3(rom_100_data), .col4(rom_101_data),
    .col5(rom_102_data), .col6(rom_103_data), .col7(rom_104_data), .col8(rom_105_data), .col9(rom_106_data),
    .col10(rom_107_data), .col11(rom_108_data), .col12(rom_109_data), .col13(rom_110_data),
    .col14(rom_111_data), .col15(rom_112_data));
  DotMatrix #(.matrixcols(16), .matrixrows(16)) dotmatrix_8 (
    .col0(rom_113_data), .col1(rom_114_data), .col2(rom_115_data), .col3(rom_116_data), .col4(rom_117_data),
    .col5(rom_118_data), .col6(rom_119_data), .col7(rom_120_data), .col8(rom_121_data), .col9(rom_122_data),
    .col10(rom_123_data), .col11(rom_124_data), .col12(rom_125_data), .col13(rom_126_data),
    .col14(rom_127_data), .col15(rom_128_data));
  DotMatrix #(.matrixcols(16), .matrixrows(16)) dotmatrix_9 (
    .col0(rom_129_data), .col1(rom_130_data), .col2(rom_131_data), .col3(rom_132_data), .col4(rom_133_data),
    .col5(rom_134_data), .col6(rom_135_data), .col7(rom_136_data), .col8(rom_137_data), .col9(rom_138_data),
    .col10(rom_139_data), .col11(rom_140_data), .col12(rom_141_data), .col13(rom_142_data),
    .col14(rom_143_data), .col15(rom_144_data));
  DotMatrix #(.matrixcols(16), .matrixrows(16)) dotmatrix_10 (
    .col0(rom_145_data), .col1(rom_146_data), .col2(rom_147_data), .col3(rom_148_data), .col4(rom_149_data),
    .col5(rom_150_data), .col6(rom_151_data), .col7(rom_152_data), .col8(rom_153_data), .col9(rom_154_data),
    .col10(rom_155_data), .col11(rom_156_data), .col12(rom_157_data), .col13(rom_158_data),
    .col14(rom_159_data), .col15(rom_160_data));

  // Notes on the sheet:
  //   contents of rom_1 (hex, n*v repeats v):
  //   10 11 7e12 4914 4978 5*4910 497f 7910 110 710 10 0 820 3020 2120 225f 2d52 2552 a492 6492 2492 2552
  //   2652 245f 2020 2820 3020 0 1 402 4404 3408 410 460 780 fc00 480 462 401 402 7fc 0 0 0 80 100 600
  //   1fff e000 5*200 ffff 4*200 0 0 80 104 20e 414 824 3044 c084 304 c04 24 14 c 6 0 0 81 82 84 feb8 9284
  //   9282 9281 92ff 9291 9291 9291 fe91 91 81 81 0 1040 1080 9100 77ff 1900 c0 0 1ff8 1110 1110 ffff 1110
  //   1110 1ff8 4*0 1c00 2c00 4000 41ec 43ec 3e00 1c00 7*0 1040 1080 1100 13ff 1c02 3082 d082 1082 1082
  //   17fe 4*1082 1002 0 200 200 4200 33fe 4 8 800 880 860 802 801 fffe 800 800 800 0 200 200 4200 33fe 4
  //   208 400 9fc 3022 c042 3082 902 402 20e 200 0 200 202 4204 33f8 4 100a 1412 1222 9142 7082 1342 1c22
  //   101a 1002 2 0 100 100 200 400 800 1000 2000 c3ff 2000 1000 800 400 200 100 100 0 0 1fff 8000 4000 0
  //   47f8 4410 4410 4410 47f8 4000 4002 4001 7ffe 0 0 101 106 7d38 5504 55fe 5522 7d22 122 400a 4fd2 5822
  //   6bc2 4822 4fd2 400a 0 0 802 804 808 808 814 8822 6842 882 902 a02 c02 802 2 2 0 1000 1000 17ff 9490
  //   7492 1491 17fe 1000 1000 13f0 3002 d001 17fe 1000 1000 0 0 0 1a 1c 12*0 400 2410 2412 2421 7ffe c440
  //   4482 402 404 ffc8 430 4428 3444 582 41f 0 2 108c 1100 1600 ffdc 1202 1102 22 7fda 4a42 4a42 4a4e
  //   7fc0 10 c 0 101 501 902 7104 1118 11e0 1100 ff00 1100 11fc 1102 1102 1102 102 10e 0 200 200 4200
  //   33fc 9 12 8f84 6898 8e0 880 18fc 2882 cf82 2 e 0 200 200 4200 33fc 9 12 8f84 6898 8e0 880 18fc 2882
  //   cf82 2 e 0 10 2010 2011 2012 fff4 5*2490 fff4 2012 2011 2010 10 0 80 100 600 1fff e100 100 3ffc 202
  //   402 fff2 802 1022 1fe2 2 1e 0 8 810 820 840 880 b00 c00 ffff c00 b00 4880 3840 820 810 8 0 200 200
  //   5*202 fffe 5*202 200 200 0 810 820 8c0 b00 ffff 900 8c0 0 7fff 4*4442 7fff 0 0 1310 1d18 f110 17ff
  //   1120 1120 101 1201 14c2 9034 7008 1034 14c2 1201 1101 0 200 200 4200 4200 4200 4202 4201 7ffe 5*4200
  //   200 200 0 10 11 7e12 4914 4978 5*4910 497f 7910 110 710 10 0 820 3020 2120 225f 2d52 2552 a492 6492
  //   2492 2552 2652 245f 2020 2820 3020 0 82 2084 2488 2491 a4a1 64d1 2791 3c91 249f 6491 a491 2491 2491
  //   2081 80 0 1040 1080 1100 13ff 1c02 3082 d082 1082 1082 17fe 4*1082 1002 0 0 3ff0 2020 3ff0 4041 4446
  //   7ff8 4442 4441 7ffe 0 7fff 4210 4d08 70f0 0 2 2 7f22 4*4922 7ffe 4*4922 7f22 2 2 0 0 0 18 24 24 18
  //   10*0 2000 2000 27ff a492 6492 2c92 3492 2492 2492 2492 6492 a492 27ff 2000 2000 0 101 501 902 7104
  //   1118 11e0 1100 ff00 1100 11fc 1102 1102 1102 102 10e 0 81 82 84 feb8 9284 9282 9281 92ff 9291 9291
  //   9291 fe91 91 81 81 0 210 4422 2841 1082 2ffc 4000 0 3ffc 2002 2002 2082 2042 3f82 2 1e 0 6*4000 7fff
  //   4000 4000 4200 4100 4080 4060 4000 4000 0 2000 2000 27ff a492 6492 2c92 3492 2492 2492 2492 6492
  //   a492 27ff 2000 2000 0 101 501 902 7104 1118 11e0 1100 ff00 1100 11fc 1102 1102 1102 102 10e 0 0 802
  //   804 808 808 814 8822 6842 882 902 a02 c02 802 2 2 0 4 7924 4924 4924 4924 7bff 4800 4800 4800 7bff
  //   4924 4924 4924 7924 4 0 0 1ffe 3084 d084 1084 1084 1ffe 200 c00 f100 10c2 1001 1002 1ffc 0 0 2000
  //   2000 27ff a492 6492 2c92 3492 2492 2492 2492 6492 a492 27ff 2000 2000 0 101 501 902 7104 1118 11e0
  //   1100 ff00 1100 11fc 1102 1102 1102 102 10e 0 0 0 da dc 12*0 10 2010 2011 2012 fff4 5*2490 fff4 2012
  //   2011 2010 10 0 40 4040 307e 180 601 102 204 c18 f060 1380 1060 1018 1404 1802 1 0 81 82 84 feb8 9284
  //   9282 9281 92ff 9291 9291 9291 fe91 91 81 81 0 210 4422 2841 1082 2ffc 4000 0 3ffc 2002 2002 2082
  //   2042 3f82 2 1e 0 6*4000 7fff 4000 4000 4200 4100 4080 4060 4000 4000 0 10 2010 2011 2012 fff4 5*2490
  //   fff4 2012 2011 2010 10 0 40 4040 307e 180 601 102 204 c18 f060 1380 1060 1018 1404 1802 1 0 0 802
  //   804 808 808 814 8822 6842 882 902 a02 c02 802 2 2 0 4 7924 4924 4924 4924 7bff 4800 4800 4800 7bff
  //   4924 4924 4924 7924 4 0 0 1ffe 3084 d084 1084 1084 1ffe 200 c00 f100 10c2 1001 1002 1ffc 0 0 10 2010
  //   2011 2012 fff4 5*2490 fff4 2012 2011 2010 10 0 40 4040 307e 180 601 102 204 c18 f060 1380 1060 1018
  //   1404 1802 1 0 0 0 da dc 12*0 204 206 3fc faa4 aaa8 aaa8 abff aa09 aae2 aa94 aa88 fab4 2c2 201 201 0
  //   2 4 18 3fe0 2400 247f 2442 2442 4442 4442 4442 c442 447f 400 400 0 81 82 84 feb8 9284 9282 9281 92ff
  //   9291 9291 9291 fe9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
  //   contents of rom_2 (hex, n*v repeats v):
  //   11 7e12 4914 4978 5*4910 497f 7910 110 710 10 0 820 3020 2120 225f 2d52 2552 a492 6492 2492 2552
  //   2652 245f 2020 2820 3020 0 1 402 4404 3408 410 460 780 fc00 480 462 401 402 7fc 0 0 0 80 100 600
  //   1fff e000 5*200 ffff 4*200 0 0 80 104 20e 414 824 3044 c084 304 c04 24 14 c 6 0 0 81 82 84 feb8 9284
  //   9282 9281 92ff 9291 9291 9291 fe91 91 81 81 0 1040 1080 9100 77ff 1900 c0 0 1ff8 1110 1110 ffff 1110
  //   1110 1ff8 4*0 1c00 2c00 4000 41ec 43ec 3e00 1c00 7*0 1040 1080 1100 13ff 1c02 3082 d082 1082 1082
  //   17fe 4*1082 1002 0 200 200 4200 33fe 4 8 800 880 860 802 801 fffe 800 800 800 0 200 200 4200 33fe 4
  //   208 400 9fc 3022 c042 3082 902 402 20e 200 0 200 202 4204 33f8 4 100a 1412 1222 9142 7082 1342 1c22
  //   101a 1002 2 0 100 100 200 400 800 1000 2000 c3ff 2000 1000 800 400 200 100 100 0 0 1fff 8000 4000 0
  //   47f8 4410 4410 4410 47f8 4000 4002 4001 7ffe 0 0 101 106 7d38 5504 55fe 5522 7d22 122 400a 4fd2 5822
  //   6bc2 4822 4fd2 400a 0 0 802 804 808 808 814 8822 6842 882 902 a02 c02 802 2 2 0 1000 1000 17ff 9490
  //   7492 1491 17fe 1000 1000 13f0 3002 d001 17fe 1000 1000 0 0 0 1a 1c 12*0 400 2410 2412 2421 7ffe c440
  //   4482 402 404 ffc8 430 4428 3444 582 41f 0 2 108c 1100 1600 ffdc 1202 1102 22 7fda 4a42 4a42 4a4e
  //   7fc0 10 c 0 101 501 902 7104 1118 11e0 1100 ff00 1100 11fc 1102 1102 1102 102 10e 0 200 200 4200
  //   33fc 9 12 8f84 6898 8e0 880 18fc 2882 cf82 2 e 0 200 200 4200 33fc 9 12 8f84 6898 8e0 880 18fc 2882
  //   cf82 2 e 0 10 2010 2011 2012 fff4 5*2490 fff4 2012 2011 2010 10 0 80 100 600 1fff e100 100 3ffc 202
  //   402 fff2 802 1022 1fe2 2 1e 0 8 810 820 840 880 b00 c00 ffff c00 b00 4880 3840 820 810 8 0 200 200
  //   5*202 fffe 5*202 200 200 0 810 820 8c0 b00 ffff 900 8c0 0 7fff 4*4442 7fff 0 0 1310 1d18 f110 17ff
  //   1120 1120 101 1201 14c2 9034 7008 1034 14c2 1201 1101 0 200 200 4200 4200 4200 4202 4201 7ffe 5*4200
  //   200 200 0 10 11 7e12 4914 4978 5*4910 497f 7910 110 710 10 0 820 3020 2120 225f 2d52 2552 a492 6492
  //   2492 2552 2652 245f 2020 2820 3020 0 82 2084 2488 2491 a4a1 64d1 2791 3c91 249f 6491 a491 2491 2491
  //   2081 80 0 1040 1080 1100 13ff 1c02 3082 d082 1082 1082 17fe 4*1082 1002 0 0 3ff0 2020 3ff0 4041 4446
  //   7ff8 4442 4441 7ffe 0 7fff 4210 4d08 70f0 0 2 2 7f22 4*4922 7ffe 4*4922 7f22 2 2 0 0 0 18 24 24 18
  //   10*0 2000 2000 27ff a492 6492 2c92 3492 2492 2492 2492 6492 a492 27ff 2000 2000 0 101 501 902 7104
  //   1118 11e0 1100 ff00 1100 11fc 1102 1102 1102 102 10e 0 81 82 84 feb8 9284 9282 9281 92ff 9291 9291
  //   9291 fe91 91 81 81 0 210 4422 2841 1082 2ffc 4000 0 3ffc 2002 2002 2082 2042 3f82 2 1e 0 6*4000 7fff
  //   4000 4000 4200 4100 4080 4060 4000 4000 0 2000 2000 27ff a492 6492 2c92 3492 2492 2492 2492 6492
  //   a492 27ff 2000 2000 0 101 501 902 7104 1118 11e0 1100 ff00 1100 11fc 1102 1102 1102 102 10e 0 0 802
  //   804 808 808 814 8822 6842 882 902 a02 c02 802 2 2 0 4 7924 4924 4924 4924 7bff 4800 4800 4800 7bff
  //   4924 4924 4924 7924 4 0 0 1ffe 3084 d084 1084 1084 1ffe 200 c00 f100 10c2 1001 1002 1ffc 0 0 2000
  //   2000 27ff a492 6492 2c92 3492 2492 2492 2492 6492 a492 27ff 2000 2000 0 101 501 902 7104 1118 11e0
  //   1100 ff00 1100 11fc 1102 1102 1102 102 10e 0 0 0 da dc 12*0 10 2010 2011 2012 fff4 5*2490 fff4 2012
  //   2011 2010 10 0 40 4040 307e 180 601 102 204 c18 f060 1380 1060 1018 1404 1802 1 0 81 82 84 feb8 9284
  //   9282 9281 92ff 9291 9291 9291 fe91 91 81 81 0 210 4422 2841 1082 2ffc 4000 0 3ffc 2002 2002 2082
  //   2042 3f82 2 1e 0 6*4000 7fff 4000 4000 4200 4100 4080 4060 4000 4000 0 10 2010 2011 2012 fff4 5*2490
  //   fff4 2012 2011 2010 10 0 40 4040 307e 180 601 102 204 c18 f060 1380 1060 1018 1404 1802 1 0 0 802
  //   804 808 808 814 8822 6842 882 902 a02 c02 802 2 2 0 4 7924 4924 4924 4924 7bff 4800 4800 4800 7bff
  //   4924 4924 4924 7924 4 0 0 1ffe 3084 d084 1084 1084 1ffe 200 c00 f100 10c2 1001 1002 1ffc 0 0 10 2010
  //   2011 2012 fff4 5*2490 fff4 2012 2011 2010 10 0 40 4040 307e 180 601 102 204 c18 f060 1380 1060 1018
  //   1404 1802 1 0 0 0 da dc 12*0 204 206 3fc faa4 aaa8 aaa8 abff aa09 aae2 aa94 aa88 fab4 2c2 201 201 0
  //   2 4 18 3fe0 2400 247f 2442 2442 4442 4442 4442 c442 447f 400 400 0 81 82 84 feb8 9284 9282 9281 92ff
  //   9291 9291 9291 fe91 9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
  //   contents of rom_3 (hex, n*v repeats v):
  //   7e12 4914 4978 5*4910 497f 7910 110 710 10 0 820 3020 2120 225f 2d52 2552 a492 6492 2492 2552 2652
  //   245f 2020 2820 3020 0 1 402 4404 3408 410 460 780 fc00 480 462 401 402 7fc 0 0 0 80 100 600 1fff
  //   e000 5*200 ffff 4*200 0 0 80 104 20e 414 824 3044 c084 304 c04 24 14 c 6 0 0 81 82 84 feb8 9284 9282
  //   9281 92ff 9291 9291 9291 fe91 91 81 81 0 1040 1080 9100 77ff 1900 c0 0 1ff8 1110 1110 ffff 1110 1110
  //   1ff8 4*0 1c00 2c00 4000 41ec 43ec 3e00 1c00 7*0 1040 1080 1100 13ff 1c02 3082 d082 1082 1082 17fe
  //   4*1082 1002 0 200 200 4200 33fe 4 8 800 880 860 802 801 fffe 800 800 800 0 200 200 4200 33fe 4 208
  //   400 9fc 3022 c042 3082 902 402 20e 200 0 200 202 4204 33f8 4 100a 1412 1222 9142 7082 1342 1c22 101a
  //   1002 2 0 100 100 200 400 800 1000 2000 c3ff 2000 1000 800 400 200 100 100 0 0 1fff 8000 4000 0 47f8
  //   4410 4410 4410 47f8 4000 4002 4001 7ffe 0 0 101 106 7d38 5504 55fe 5522 7d22 122 400a 4fd2 5822 6bc2
  //   4822 4fd2 400a 0 0 802 804 808 808 814 8822 6842 882 902 a02 c02 802 2 2 0 1000 1000 17ff 9490 7492
  //   1491 17fe 1000 1000 13f0 3002 d001 17fe 1000 1000 0 0 0 1a 1c 12*0 400 2410 2412 2421 7ffe c440 4482
  //   402 404 ffc8 430 4428 3444 582 41f 0 2 108c 1100 1600 ffdc 1202 1102 22 7fda 4a42 4a42 4a4e 7fc0 10
  //   c 0 101 501 902 7104 1118 11e0 1100 ff00 1100 11fc 1102 1102 1102 102 10e 0 200 200 4200 33fc 9 12
  //   8f84 6898 8e0 880 18fc 2882 cf82 2 e 0 200 200 4200 33fc 9 12 8f84 6898 8e0 880 18fc 2882 cf82 2 e 0
  //   10 2010 2011 2012 fff4 5*2490 fff4 2012 2011 2010 10 0 80 100 600 1fff e100 100 3ffc 202 402 fff2
  //   802 1022 1fe2 2 1e 0 8 810 820 840 880 b00 c00 ffff c00 b00 4880 3840 820 810 8 0 200 200 5*202 fffe
  //   5*202 200 200 0 810 820 8c0 b00 ffff 900 8c0 0 7fff 4*4442 7fff 0 0 1310 1d18 f110 17ff 1120 1120
  //   101 1201 14c2 9034 7008 1034 14c2 1201 1101 0 200 200 4200 4200 4200 4202 4201 7ffe 5*4200 200 200 0
  //   10 11 7e12 4914 4978 5*4910 497f 7910 110 710 10 0 820 3020 2120 225f 2d52 2552 a492 6492 2492 2552
  //   2652 245f 2020 2820 3020 0 82 2084 2488 2491 a4a1 64d1 2791 3c91 249f 6491 a491 2491 2491 2081 80 0
  //   1040 1080 1100 13ff 1c02 3082 d082 1082 1082 17fe 4*1082 1002 0 0 3ff0 2020 3ff0 4041 4446 7ff8 4442
  //   4441 7ffe 0 7fff 4210 4d08 70f0 0 2 2 7f22 4*4922 7ffe 4*4922 7f22 2 2 0 0 0 18 24 24 18 10*0 2000
  //   2000 27ff a492 6492 2c92 3492 2492 2492 2492 6492 a492 27ff 2000 2000 0 101 501 902 7104 1118 11e0
  //   1100 ff00 1100 11fc 1102 1102 1102 102 10e 0 81 82 84 feb8 9284 9282 9281 92ff 9291 9291 9291 fe91
  //   91 81 81 0 210 4422 2841 1082 2ffc 4000 0 3ffc 2002 2002 2082 2042 3f82 2 1e 0 6*4000 7fff 4000 4000
  //   4200 4100 4080 4060 4000 4000 0 2000 2000 27ff a492 6492 2c92 3492 2492 2492 2492 6492 a492 27ff
  //   2000 2000 0 101 501 902 7104 1118 11e0 1100 ff00 1100 11fc 1102 1102 1102 102 10e 0 0 802 804 808
  //   808 814 8822 6842 882 902 a02 c02 802 2 2 0 4 7924 4924 4924 4924 7bff 4800 4800 4800 7bff 4924 4924
  //   4924 7924 4 0 0 1ffe 3084 d084 1084 1084 1ffe 200 c00 f100 10c2 1001 1002 1ffc 0 0 2000 2000 27ff
  //   a492 6492 2c92 3492 2492 2492 2492 6492 a492 27ff 2000 2000 0 101 501 902 7104 1118 11e0 1100 ff00
  //   1100 11fc 1102 1102 1102 102 10e 0 0 0 da dc 12*0 10 2010 2011 2012 fff4 5*2490 fff4 2012 2011 2010
  //   10 0 40 4040 307e 180 601 102 204 c18 f060 1380 1060 1018 1404 1802 1 0 81 82 84 feb8 9284 9282 9281
  //   92ff 9291 9291 9291 fe91 91 81 81 0 210 4422 2841 1082 2ffc 4000 0 3ffc 2002 2002 2082 2042 3f82 2
  //   1e 0 6*4000 7fff 4000 4000 4200 4100 4080 4060 4000 4000 0 10 2010 2011 2012 fff4 5*2490 fff4 2012
  //   2011 2010 10 0 40 4040 307e 180 601 102 204 c18 f060 1380 1060 1018 1404 1802 1 0 0 802 804 808 808
  //   814 8822 6842 882 902 a02 c02 802 2 2 0 4 7924 4924 4924 4924 7bff 4800 4800 4800 7bff 4924 4924
  //   4924 7924 4 0 0 1ffe 3084 d084 1084 1084 1ffe 200 c00 f100 10c2 1001 1002 1ffc 0 0 10 2010 2011 2012
  //   fff4 5*2490 fff4 2012 2011 2010 10 0 40 4040 307e 180 601 102 204 c18 f060 1380 1060 1018 1404 1802
  //   1 0 0 0 da dc 12*0 204 206 3fc faa4 aaa8 aaa8 abff aa09 aae2 aa94 aa88 fab4 2c2 201 201 0 2 4 18
  //   3fe0 2400 247f 2442 2442 4442 4442 4442 c442 447f 400 400 0 81 82 84 feb8 9284 9282 9281 92ff 9291
  //   9291 9291 fe91 91 8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
  //   contents of rom_4 (hex, n*v repeats v):
  //   4914 4978 5*4910 497f 7910 110 710 10 0 820 3020 2120 225f 2d52 2552 a492 6492 2492 2552 2652 245f
  //   2020 2820 3020 0 1 402 4404 3408 410 460 780 fc00 480 462 401 402 7fc 0 0 0 80 100 600 1fff e000
  //   5*200 ffff 4*200 0 0 80 104 20e 414 824 3044 c084 304 c04 24 14 c 6 0 0 81 82 84 feb8 9284 9282 9281
  //   92ff 9291 9291 9291 fe91 91 81 81 0 1040 1080 9100 77ff 1900 c0 0 1ff8 1110 1110 ffff 1110 1110 1ff8
  //   4*0 1c00 2c00 4000 41ec 43ec 3e00 1c00 7*0 1040 1080 1100 13ff 1c02 3082 d082 1082 1082 17fe 4*1082
  //   1002 0 200 200 4200 33fe 4 8 800 880 860 802 801 fffe 800 800 800 0 200 200 4200 33fe 4 208 400 9fc
  //   3022 c042 3082 902 402 20e 200 0 200 202 4204 33f8 4 100a 1412 1222 9142 7082 1342 1c22 101a 1002 2
  //   0 100 100 200 400 800 1000 2000 c3ff 2000 1000 800 400 200 100 100 0 0 1fff 8000 4000 0 47f8 4410
  //   4410 4410 47f8 4000 4002 4001 7ffe 0 0 101 106 7d38 5504 55fe 5522 7d22 122 400a 4fd2 5822 6bc2 4822
  //   4fd2 400a 0 0 802 804 808 808 814 8822 6842 882 902 a02 c02 802 2 2 0 1000 1000 17ff 9490 7492 1491
  //   17fe 1000 1000 13f0 3002 d001 17fe 1000 1000 0 0 0 1a 1c 12*0 400 2410 2412 2421 7ffe c440 4482 402
  //   404 ffc8 430 4428 3444 582 41f 0 2 108c 1100 1600 ffdc 1202 1102 22 7fda 4a42 4a42 4a4e 7fc0 10 c 0
  //   101 501 902 7104 1118 11e0 1100 ff00 1100 11fc 1102 1102 1102 102 10e 0 200 200 4200 33fc 9 12 8f84
  //   6898 8e0 880 18fc 2882 cf82 2 e 0 200 200 4200 33fc 9 12 8f84 6898 8e0 880 18fc 2882 cf82 2 e 0 10
  //   2010 2011 2012 fff4 5*2490 fff4 2012 2011 2010 10 0 80 100 600 1fff e100 100 3ffc 202 402 fff2 802
  //   1022 1fe2 2 1e 0 8 810 820 840 880 b00 c00 ffff c00 b00 4880 3840 820 810 8 0 200 200 5*202 fffe
  //   5*202 200 200 0 810 820 8c0 b00 ffff 900 8c0 0 7fff 4*4442 7fff 0 0 1310 1d18 f110 17ff 1120 1120
  //   101 1201 14c2 9034 7008 1034 14c2 1201 1101 0 200 200 4200 4200 4200 4202 4201 7ffe 5*4200 200 200 0
  //   10 11 7e12 4914 4978 5*4910 497f 7910 110 710 10 0 820 3020 2120 225f 2d52 2552 a492 6492 2492 2552
  //   2652 245f 2020 2820 3020 0 82 2084 2488 2491 a4a1 64d1 2791 3c91 249f 6491 a491 2491 2491 2081 80 0
  //   1040 1080 1100 13ff 1c02 3082 d082 1082 1082 17fe 4*1082 1002 0 0 3ff0 2020 3ff0 4041 4446 7ff8 4442
  //   4441 7ffe 0 7fff 4210 4d08 70f0 0 2 2 7f22 4*4922 7ffe 4*4922 7f22 2 2 0 0 0 18 24 24 18 10*0 2000
  //   2000 27ff a492 6492 2c92 3492 2492 2492 2492 6492 a492 27ff 2000 2000 0 101 501 902 7104 1118 11e0
  //   1100 ff00 1100 11fc 1102 1102 1102 102 10e 0 81 82 84 feb8 9284 9282 9281 92ff 9291 9291 9291 fe91
  //   91 81 81 0 210 4422 2841 1082 2ffc 4000 0 3ffc 2002 2002 2082 2042 3f82 2 1e 0 6*4000 7fff 4000 4000
  //   4200 4100 4080 4060 4000 4000 0 2000 2000 27ff a492 6492 2c92 3492 2492 2492 2492 6492 a492 27ff
  //   2000 2000 0 101 501 902 7104 1118 11e0 1100 ff00 1100 11fc 1102 1102 1102 102 10e 0 0 802 804 808
  //   808 814 8822 6842 882 902 a02 c02 802 2 2 0 4 7924 4924 4924 4924 7bff 4800 4800 4800 7bff 4924 4924
  //   4924 7924 4 0 0 1ffe 3084 d084 1084 1084 1ffe 200 c00 f100 10c2 1001 1002 1ffc 0 0 2000 2000 27ff
  //   a492 6492 2c92 3492 2492 2492 2492 6492 a492 27ff 2000 2000 0 101 501 902 7104 1118 11e0 1100 ff00
  //   1100 11fc 1102 1102 1102 102 10e 0 0 0 da dc 12*0 10 2010 2011 2012 fff4 5*2490 fff4 2012 2011 2010
  //   10 0 40 4040 307e 180 601 102 204 c18 f060 1380 1060 1018 1404 1802 1 0 81 82 84 feb8 9284 9282 9281
  //   92ff 9291 9291 9291 fe91 91 81 81 0 210 4422 2841 1082 2ffc 4000 0 3ffc 2002 2002 2082 2042 3f82 2
  //   1e 0 6*4000 7fff 4000 4000 4200 4100 4080 4060 4000 4000 0 10 2010 2011 2012 fff4 5*2490 fff4 2012
  //   2011 2010 10 0 40 4040 307e 180 601 102 204 c18 f060 1380 1060 1018 1404 1802 1 0 0 802 804 808 808
  //   814 8822 6842 882 902 a02 c02 802 2 2 0 4 7924 4924 4924 4924 7bff 4800 4800 4800 7bff 4924 4924
  //   4924 7924 4 0 0 1ffe 3084 d084 1084 1084 1ffe 200 c00 f100 10c2 1001 1002 1ffc 0 0 10 2010 2011 2012
  //   fff4 5*2490 fff4 2012 2011 2010 10 0 40 4040 307e 180 601 102 204 c18 f060 1380 1060 1018 1404 1802
  //   1 0 0 0 da dc 12*0 204 206 3fc faa4 aaa8 aaa8 abff aa09 aae2 aa94 aa88 fab4 2c2 201 201 0 2 4 18
  //   3fe0 2400 247f 2442 2442 4442 4442 4442 c442 447f 400 400 0 81 82 84 feb8 9284 9282 9281 92ff 9291
  //   9291 9291 fe91 91 81 81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
  //   contents of rom_5 (hex, n*v repeats v):
  //   4978 5*4910 497f 7910 110 710 10 0 820 3020 2120 225f 2d52 2552 a492 6492 2492 2552 2652 245f 2020
  //   2820 3020 0 1 402 4404 3408 410 460 780 fc00 480 462 401 402 7fc 0 0 0 80 100 600 1fff e000 5*200
  //   ffff 4*200 0 0 80 104 20e 414 824 3044 c084 304 c04 24 14 c 6 0 0 81 82 84 feb8 9284 9282 9281 92ff
  //   929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
  //   contents of rom_6 (hex, n*v repeats v):
  //   5*4910 497f 7910 110 710 10 0 820 3020 2120 225f 2d52 2552 a492 6492 2492 2552 2652 245f 2020 2820
  //   3020 0 1 402 4404 3408 410 460 780 fc00 480 462 401 402 7fc 0 0 0 80 100 600 1fff e000 5*200 ffff
  //   4*200 0 0 80 104 20e 414 824 3044 c084 304 c04 24 14 c 6 0 0 81 82 84 feb8 9284 9282 9281 92ff 9291
  //   929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
  //   contents of rom_7 (hex, n*v repeats v):
  //   4*4910 497f 7910 110 710 10 0 820 3020 2120 225f 2d52 2552 a492 6492 2492 2552 2652 245f 2020 2820
  //   3020 0 1 402 4404 3408 410 460 780 fc00 480 462 401 402 7fc 0 0 0 80 100 600 1fff e000 5*200 ffff
  //   4*200 0 0 80 104 20e 414 824 3044 c084 304 c04 24 14 c 6 0 0 81 82 84 feb8 9284 9282 9281 92ff 9291
  //   929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
  //   contents of rom_8 (hex, n*v repeats v):
  //   4910 4910 4910 497f 7910 110 710 10 0 820 3020 2120 225f 2d52 2552 a492 6492 2492 2552 2652 245f
  //   2020 2820 3020 0 1 402 4404 3408 410 460 780 fc00 480 462 401 402 7fc 0 0 0 80 100 600 1fff e000
  //   5*200 ffff 4*200 0 0 80 104 20e 414 824 3044 c084 304 c04 24 14 c 6 0 0 81 82 84 feb8 9284 9282 9281
  //   92ff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
  //   contents of rom_9 (hex, n*v repeats v):
  //   4910 4910 497f 7910 110 710 10 0 820 3020 2120 225f 2d52 2552 a492 6492 2492 2552 2652 245f 2020
  //   2820 3020 0 1 402 4404 3408 410 460 780 fc00 480 462 401 402 7fc 0 0 0 80 100 600 1fff e000 5*200
  //   ffff 4*200 0 0 80 104 20e 414 824 3044 c084 304 c04 24 14 c 6 0 0 81 82 84 feb8 9284 9282 9281 92ff
  //   9291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
  //   contents of rom_10 (hex, n*v repeats v):
  //   4910 497f 7910 110 710 10 0 820 3020 2120 225f 2d52 2552 a492 6492 2492 2552 2652 245f 2020 2820
  //   3020 0 1 402 4404 3408 410 460 780 fc00 480 462 401 402 7fc 0 0 0 80 100 600 1fff e000 5*200 ffff
  //   4*200 0 0 80 104 20e 414 824 3044 c084 304 c04 24 14 c 6 0 0 81 82 84 feb8 9284 9282 9281 92ff 9291
  //   9291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
  //   contents of rom_11 (hex, n*v repeats v):
  //   497f 7910 110 710 10 0 820 3020 2120 225f 2d52 2552 a492 6492 2492 2552 2652 245f 2020 2820 3020 0 1
  //   402 4404 3408 410 460 780 fc00 480 462 401 402 7fc 0 0 0 80 100 600 1fff e000 5*200 ffff 4*200 0 0
  //   80 104 20e 414 824 3044 c084 304 c04 24 14 c 6 0 0 81 82 84 feb8 9284 9282 9281 92ff 9291 9291 9291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
  //   contents of rom_12 (hex, n*v repeats v):
  //   7910 110 710 10 0 820 3020 2120 225f 2d52 2552 a492 6492 2492 2552 2652 245f 2020 2820 3020 0 1 402
  //   4404 3408 410 460 780 fc00 480 462 401 402 7fc 0 0 0 80 100 600 1fff e000 5*200 ffff 4*200 0 0 80
  //   104 20e 414 824 3044 c084 304 c04 24 14 c 6 0 0 81 82 84 feb8 9284 9282 9281 92ff 9291 9291 9291
  //   fe91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
  //   contents of rom_13 (hex, n*v repeats v):
  //   110 710 10 0 820 3020 2120 225f 2d52 2552 a492 6492 2492 2552 2652 245f 2020 2820 3020 0 1 402 4404
  //   3408 410 460 780 fc00 480 462 401 402 7fc 0 0 0 80 100 600 1fff e000 5*200 ffff 4*200 0 0 80 104 20e
  //   414 824 3044 c084 304 c04 24 14 c 6 0 0 81 82 84 feb8 9284 9282 9281 92ff 9291 9291 9291 fe91 91 81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
  //   contents of rom_14 (hex, n*v repeats v):
  //   710 10 0 820 3020 2120 225f 2d52 2552 a492 6492 2492 2552 2652 245f 2020 2820 3020 0 1 402 4404 3408
  //   410 460 780 fc00 480 462 401 402 7fc 0 0 0 80 100 600 1fff e000 5*200 ffff 4*200 0 0 80 104 20e 414
  //   824 3044 c084 304 c04 24 14 c 6 0 0 81 82 84 feb8 9284 9282 9281 92ff 9291 9291 9291 fe91 91 81 81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
  //   contents of rom_15 (hex, n*v repeats v):
  //   10 0 820 3020 2120 225f 2d52 2552 a492 6492 2492 2552 2652 245f 2020 2820 3020 0 1 402 4404 3408 410
  //   460 780 fc00 480 462 401 402 7fc 0 0 0 80 100 600 1fff e000 5*200 ffff 4*200 0 0 80 104 20e 414 824
  //   3044 c084 304 c04 24 14 c 6 0 0 81 82 84 feb8 9284 9282 9281 92ff 9291 9291 9291 fe91 91 81 81 0 10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
  //   contents of rom_16 (hex, n*v repeats v):
  //   0 820 3020 2120 225f 2d52 2552 a492 6492 2492 2552 2652 245f 2020 2820 3020 0 1 402 4404 3408 410
  //   460 780 fc00 480 462 401 402 7fc 0 0 0 80 100 600 1fff e000 5*200 ffff 4*200 0 0 80 104 20e 414 824
  //   3044 c084 304 c04 24 14 c 6 0 0 81 82 84 feb8 9284 9282 9281 92ff 9291 9291 9291 fe91 91 81 81 0
  //   1040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
  //   contents of rom_17 (hex, n*v repeats v):
  //   820 3020 2120 225f 2d52 2552 a492 6492 2492 2552 2652 245f 2020 2820 3020 0 1 402 4404 3408 410 460
  //   780 fc00 480 462 401 402 7fc 0 0 0 80 100 600 1fff e000 5*200 ffff 4*200 0 0 80 104 20e 414 824 3044
  //   c084 304 c04 24 14 c 6 0 0 81 82 84 feb8 9284 9282 9281 92ff 9291 9291 9291 fe91 91 81 81 0 1040 10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
  //   contents of rom_18 (hex, n*v repeats v):
  //   3020 2120 225f 2d52 2552 a492 6492 2492 2552 2652 245f 2020 2820 3020 0 1 402 4404 3408 410 460 780
  //   fc00 480 462 401 402 7fc 0 0 0 80 100 600 1fff e000 5*200 ffff 4*200 0 0 80 104 20e 414 824 3044
  //   c084 304 c04 24 14 c 6 0 0 81 82 84 feb8 9284 9282 9281 92ff 9291 9291 9291 fe91 91 81 81 0 1040
  //   1080 9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
  //   contents of rom_19 (hex, n*v repeats v):
  //   2120 225f 2d52 2552 a492 6492 2492 2552 2652 245f 2020 2820 3020 0 1 402 4404 3408 410 460 780 fc00
  //   480 462 401 402 7fc 0 0 0 80 100 600 1fff e000 5*200 ffff 4*200 0 0 80 104 20e 414 824 3044 c084 304
  //   c04 24 14 c 6 0 0 81 82 84 feb8 9284 9282 9281 92ff 9291 9291 9291 fe91 91 81 81 0 1040 1080 9100 7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
  //   contents of rom_20 (hex, n*v repeats v):
  //   225f 2d52 2552 a492 6492 2492 2552 2652 245f 2020 2820 3020 0 1 402 4404 3408 410 460 780 fc00 480
  //   462 401 402 7fc 0 0 0 80 100 600 1fff e000 5*200 ffff 4*200 0 0 80 104 20e 414 824 3044 c084 304 c04
  //   24 14 c 6 0 0 81 82 84 feb8 9284 9282 9281 92ff 9291 9291 9291 fe91 91 81 81 0 1040 1080 9100 77ff 1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
  //   contents of rom_21 (hex, n*v repeats v):
  //   2d52 2552 a492 6492 2492 2552 2652 245f 2020 2820 3020 0 1 402 4404 3408 410 460 780 fc00 480 462
  //   401 402 7fc 0 0 0 80 100 600 1fff e000 5*200 ffff 4*200 0 0 80 104 20e 414 824 3044 c084 304 c04 24
  //   14 c 6 0 0 81 82 84 feb8 9284 9282 9281 92ff 9291 9291 9291 fe91 91 81 81 0 1040 1080 9100 77ff 1900
  //   c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
  //   contents of rom_22 (hex, n*v repeats v):
  //   2552 a492 6492 2492 2552 2652 245f 2020 2820 3020 0 1 402 4404 3408 410 460 780 fc00 480 462 401 402
  //   7fc 0 0 0 80 100 600 1fff e000 5*200 ffff 4*200 0 0 80 104 20e 414 824 3044 c084 304 c04 24 14 c 6 0
  //   0 81 82 84 feb8 9284 9282 9281 92ff 9291 9291 9291 fe91 91 81 81 0 1040 1080 9100 77ff 1900 c0 0 1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
  //   contents of rom_23 (hex, n*v repeats v):
  //   a492 6492 2492 2552 2652 245f 2020 2820 3020 0 1 402 4404 3408 410 460 780 fc00 480 462 401 402 7fc
  //   0 0 0 80 100 600 1fff e000 5*200 ffff 4*200 0 0 80 104 20e 414 824 3044 c084 304 c04 24 14 c 6 0 0
  //   81 82 84 feb8 9284 9282 9281 92ff 9291 9291 9291 fe91 91 81 81 0 1040 1080 9100 77ff 1900 c0 0 1ff8
  //   1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
  //   contents of rom_24 (hex, n*v repeats v):
  //   6492 2492 2552 2652 245f 2020 2820 3020 0 1 402 4404 3408 410 460 780 fc00 480 462 401 402 7fc 0 0 0
  //   80 100 600 1fff e000 5*200 ffff 4*200 0 0 80 104 20e 414 824 3044 c084 304 c04 24 14 c 6 0 0 81 82
  //   84 feb8 9284 9282 9281 92ff 9291 9291 9291 fe91 91 81 81 0 1040 1080 9100 77ff 1900 c0 0 1ff8 1110 1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
  //   contents of rom_25 (hex, n*v repeats v):
  //   2492 2552 2652 245f 2020 2820 3020 0 1 402 4404 3408 410 460 780 fc00 480 462 401 402 7fc 0 0 0 80
  //   100 600 1fff e000 5*200 ffff 4*200 0 0 80 104 20e 414 824 3044 c084 304 c04 24 14 c 6 0 0 81 82 84
  //   feb8 9284 9282 9281 92ff 9291 9291 9291 fe91 91 81 81 0 1040 1080 9100 77ff 1900 c0 0 1ff8 1110 1110
  //   f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
  //   contents of rom_26 (hex, n*v repeats v):
  //   2552 2652 245f 2020 2820 3020 0 1 402 4404 3408 410 460 780 fc00 480 462 401 402 7fc 0 0 0 80 100
  //   600 1fff e000 5*200 ffff 4*200 0 0 80 104 20e 414 824 3044 c084 304 c04 24 14 c 6 0 0 81 82 84 feb8
  //   9284 9282 9281 92ff 9291 9291 9291 fe91 91 81 81 0 1040 1080 9100 77ff 1900 c0 0 1ff8 1110 1110 ffff
  //   1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
  //   contents of rom_27 (hex, n*v repeats v):
  //   2652 245f 2020 2820 3020 0 1 402 4404 3408 410 460 780 fc00 480 462 401 402 7fc 0 0 0 80 100 600
  //   1fff e000 5*200 ffff 4*200 0 0 80 104 20e 414 824 3044 c084 304 c04 24 14 c 6 0 0 81 82 84 feb8 9284
  //   9282 9281 92ff 9291 9291 9291 fe91 91 81 81 0 1040 1080 9100 77ff 1900 c0 0 1ff8 1110 1110 ffff 1110
  //   1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
  //   contents of rom_28 (hex, n*v repeats v):
  //   245f 2020 2820 3020 0 1 402 4404 3408 410 460 780 fc00 480 462 401 402 7fc 0 0 0 80 100 600 1fff
  //   e000 5*200 ffff 4*200 0 0 80 104 20e 414 824 3044 c084 304 c04 24 14 c 6 0 0 81 82 84 feb8 9284 9282
  //   9281 92ff 9291 9291 9291 fe91 91 81 81 0 1040 1080 9100 77ff 1900 c0 0 1ff8 1110 1110 ffff 1110 1110
  //   1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
  //   contents of rom_29 (hex, n*v repeats v):
  //   2020 2820 3020 0 1 402 4404 3408 410 460 780 fc00 480 462 401 402 7fc 0 0 0 80 100 600 1fff e000
  //   5*200 ffff 4*200 0 0 80 104 20e 414 824 3044 c084 304 c04 24 14 c 6 0 0 81 82 84 feb8 9284 9282 9281
  //   92ff 9291 9291 9291 fe91 91 81 81 0 1040 1080 9100 77ff 1900 c0 0 1ff8 1110 1110 ffff 1110 1110 1ff8
  //   4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
  //   contents of rom_30 (hex, n*v repeats v):
  //   2820 3020 0 1 402 4404 3408 410 460 780 fc00 480 462 401 402 7fc 0 0 0 80 100 600 1fff e000 5*200
  //   ffff 4*200 0 0 80 104 20e 414 824 3044 c084 304 c04 24 14 c 6 0 0 81 82 84 feb8 9284 9282 9281 92ff
  //   9291 9291 9291 fe91 91 81 81 0 1040 1080 9100 77ff 1900 c0 0 1ff8 1110 1110 ffff 1110 1110 1ff8 4*0
  //   1c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
  //   contents of rom_31 (hex, n*v repeats v):
  //   3020 0 1 402 4404 3408 410 460 780 fc00 480 462 401 402 7fc 0 0 0 80 100 600 1fff e000 5*200 ffff
  //   4*200 0 0 80 104 20e 414 824 3044 c084 304 c04 24 14 c 6 0 0 81 82 84 feb8 9284 9282 9281 92ff 9291
  //   9291 9291 fe91 91 81 81 0 1040 1080 9100 77ff 1900 c0 0 1ff8 1110 1110 ffff 1110 1110 1ff8 4*0 1c00
  //   2c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
  //   contents of rom_32 (hex, n*v repeats v):
  //   0 1 402 4404 3408 410 460 780 fc00 480 462 401 402 7fc 0 0 0 80 100 600 1fff e000 5*200 ffff 4*200 0
  //   0 80 104 20e 414 824 3044 c084 304 c04 24 14 c 6 0 0 81 82 84 feb8 9284 9282 9281 92ff 9291 9291
  //   9291 fe91 91 81 81 0 1040 1080 9100 77ff 1900 c0 0 1ff8 1110 1110 ffff 1110 1110 1ff8 4*0 1c00 2c00
  //   40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
  //   contents of rom_33 (hex, n*v repeats v):
  //   1 402 4404 3408 410 460 780 fc00 480 462 401 402 7fc 0 0 0 80 100 600 1fff e000 5*200 ffff 4*200 0 0
  //   80 104 20e 414 824 3044 c084 304 c04 24 14 c 6 0 0 81 82 84 feb8 9284 9282 9281 92ff 9291 9291 9291
  //   fe91 91 81 81 0 1040 1080 9100 77ff 1900 c0 0 1ff8 1110 1110 ffff 1110 1110 1ff8 4*0 1c00 2c00 4000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
  //   contents of rom_34 (hex, n*v repeats v):
  //   402 4404 3408 410 460 780 fc00 480 462 401 402 7fc 0 0 0 80 100 600 1fff e000 5*200 ffff 4*200 0 0
  //   80 104 20e 414 824 3044 c084 304 c04 24 14 c 6 0 0 81 82 84 feb8 9284 9282 9281 92ff 9291 9291 9291
  //   fe91 91 81 81 0 1040 1080 9100 77ff 1900 c0 0 1ff8 1110 1110 ffff 1110 1110 1ff8 4*0 1c00 2c00 4000
  //   4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
  //   contents of rom_35 (hex, n*v repeats v):
  //   4404 3408 410 460 780 fc00 480 462 401 402 7fc 0 0 0 80 100 600 1fff e000 5*200 ffff 4*200 0 0 80
  //   104 20e 414 824 3044 c084 304 c04 24 14 c 6 0 0 81 82 84 feb8 9284 9282 9281 92ff 9291 9291 9291
  //   fe91 91 81 81 0 1040 1080 9100 77ff 1900 c0 0 1ff8 1110 1110 ffff 1110 1110 1ff8 4*0 1c00 2c00 4000
  //   41ec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
  //   contents of rom_36 (hex, n*v repeats v):
  //   3408 410 460 780 fc00 480 462 401 402 7fc 0 0 0 80 100 600 1fff e000 5*200 ffff 4*200 0 0 80 104 20e
  //   414 824 3044 c084 304 c04 24 14 c 6 0 0 81 82 84 feb8 9284 9282 9281 92ff 9291 9291 9291 fe91 91 81
  //   81 0 1040 1080 9100 77ff 1900 c0 0 1ff8 1110 1110 ffff 1110 1110 1ff8 4*0 1c00 2c00 4000 41ec 43ec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
  //   contents of rom_37 (hex, n*v repeats v):
  //   410 460 780 fc00 480 462 401 402 7fc 0 0 0 80 100 600 1fff e000 5*200 ffff 4*200 0 0 80 104 20e 414
  //   824 3044 c084 304 c04 24 14 c 6 0 0 81 82 84 feb8 9284 9282 9281 92ff 9291 9291 9291 fe91 91 81 81 0
  //   1040 1080 9100 77ff 1900 c0 0 1ff8 1110 1110 ffff 1110 1110 1ff8 4*0 1c00 2c00 4000 41ec 43ec 3e00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
  //   contents of rom_38 (hex, n*v repeats v):
  //   460 780 fc00 480 462 401 402 7fc 0 0 0 80 100 600 1fff e000 5*200 ffff 4*200 0 0 80 104 20e 414 824
  //   3044 c084 304 c04 24 14 c 6 0 0 81 82 84 feb8 9284 9282 9281 92ff 9291 9291 9291 fe91 91 81 81 0
  //   1040 1080 9100 77ff 1900 c0 0 1ff8 1110 1110 ffff 1110 1110 1ff8 4*0 1c00 2c00 4000 41ec 43ec 3e00
  //   1c00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
  //   contents of rom_39 (hex, n*v repeats v):
  //   780 fc00 480 462 401 402 7fc 0 0 0 80 100 600 1fff e000 5*200 ffff 4*200 0 0 80 104 20e 414 824 3044
  //   c084 304 c04 24 14 c 6 0 0 81 82 84 feb8 9284 9282 9281 92ff 9291 9291 9291 fe91 91 81 81 0 1040
  //   1080 9100 77ff 1900 c0 0 1ff8 1110 1110 ffff 1110 1110 1ff8 4*0 1c00 2c00 4000 41ec 43ec 3e00 1c00
  //   7*0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
  //   contents of rom_40 (hex, n*v repeats v):
  //   fc00 480 462 401 402 7fc 0 0 0 80 100 600 1fff e000 5*200 ffff 4*200 0 0 80 104 20e 414 824 3044
  //   c084 304 c04 24 14 c 6 0 0 81 82 84 feb8 9284 9282 9281 92ff 9291 9291 9291 fe91 91 81 81 0 1040
  //   1080 9100 77ff 1900 c0 0 1ff8 1110 1110 ffff 1110 1110 1ff8 4*0 1c00 2c00 4000 41ec 43ec 3e00 1c00
  //   7*0 104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
  //   contents of rom_41 (hex, n*v repeats v):
  //   480 462 401 402 7fc 0 0 0 80 100 600 1fff e000 5*200 ffff 4*200 0 0 80 104 20e 414 824 3044 c084 304
  //   c04 24 14 c 6 0 0 81 82 84 feb8 9284 9282 9281 92ff 9291 9291 9291 fe91 91 81 81 0 1040 1080 9100
  //   77ff 1900 c0 0 1ff8 1110 1110 ffff 1110 1110 1ff8 4*0 1c00 2c00 4000 41ec 43ec 3e00 1c00 7*0 1040
  //   108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
  //   contents of rom_42 (hex, n*v repeats v):
  //   462 401 402 7fc 0 0 0 80 100 600 1fff e000 5*200 ffff 4*200 0 0 80 104 20e 414 824 3044 c084 304 c04
  //   24 14 c 6 0 0 81 82 84 feb8 9284 9282 9281 92ff 9291 9291 9291 fe91 91 81 81 0 1040 1080 9100 77ff
  //   1900 c0 0 1ff8 1110 1110 ffff 1110 1110 1ff8 4*0 1c00 2c00 4000 41ec 43ec 3e00 1c00 7*0 1040 1080 11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
  //   contents of rom_43 (hex, n*v repeats v):
  //   401 402 7fc 0 0 0 80 100 600 1fff e000 5*200 ffff 4*200 0 0 80 104 20e 414 824 3044 c084 304 c04 24
  //   14 c 6 0 0 81 82 84 feb8 9284 9282 9281 92ff 9291 9291 9291 fe91 91 81 81 0 1040 1080 9100 77ff 1900
  //   c0 0 1ff8 1110 1110 ffff 1110 1110 1ff8 4*0 1c00 2c00 4000 41ec 43ec 3e00 1c00 7*0 1040 1080 1100 1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
  //   contents of rom_44 (hex, n*v repeats v):
  //   402 7fc 0 0 0 80 100 600 1fff e000 5*200 ffff 4*200 0 0 80 104 20e 414 824 3044 c084 304 c04 24 14 c
  //   6 0 0 81 82 84 feb8 9284 9282 9281 92ff 9291 9291 9291 fe91 91 81 81 0 1040 1080 9100 77ff 1900 c0 0
  //   1ff8 1110 1110 ffff 1110 1110 1ff8 4*0 1c00 2c00 4000 41ec 43ec 3e00 1c00 7*0 1040 1080 1100 13ff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
  //   contents of rom_45 (hex, n*v repeats v):
  //   7fc 0 0 0 80 100 600 1fff e000 5*200 ffff 4*200 0 0 80 104 20e 414 824 3044 c084 304 c04 24 14 c 6 0
  //   0 81 82 84 feb8 9284 9282 9281 92ff 9291 9291 9291 fe91 91 81 81 0 1040 1080 9100 77ff 1900 c0 0
  //   1ff8 1110 1110 ffff 1110 1110 1ff8 4*0 1c00 2c00 4000 41ec 43ec 3e00 1c00 7*0 1040 1080 1100 13ff
  //   1c02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
  //   contents of rom_46 (hex, n*v repeats v):
  //   0 0 0 80 100 600 1fff e000 5*200 ffff 4*200 0 0 80 104 20e 414 824 3044 c084 304 c04 24 14 c 6 0 0
  //   81 82 84 feb8 9284 9282 9281 92ff 9291 9291 9291 fe91 91 81 81 0 1040 1080 9100 77ff 1900 c0 0 1ff8
  //   1110 1110 ffff 1110 1110 1ff8 4*0 1c00 2c00 4000 41ec 43ec 3e00 1c00 7*0 1040 1080 1100 13ff 1c02
  //   308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
  //   contents of rom_47 (hex, n*v repeats v):
  //   0 0 80 100 600 1fff e000 5*200 ffff 4*200 0 0 80 104 20e 414 824 3044 c084 304 c04 24 14 c 6 0 0 81
  //   82 84 feb8 9284 9282 9281 92ff 9291 9291 9291 fe91 91 81 81 0 1040 1080 9100 77ff 1900 c0 0 1ff8
  //   1110 1110 ffff 1110 1110 1ff8 4*0 1c00 2c00 4000 41ec 43ec 3e00 1c00 7*0 1040 1080 1100 13ff 1c02
  //   3082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
  //   contents of rom_48 (hex, n*v repeats v):
  //   0 80 100 600 1fff e000 5*200 ffff 4*200 0 0 80 104 20e 414 824 3044 c084 304 c04 24 14 c 6 0 0 81 82
  //   84 feb8 9284 9282 9281 92ff 9291 9291 9291 fe91 91 81 81 0 1040 1080 9100 77ff 1900 c0 0 1ff8 1110
  //   1110 ffff 1110 1110 1ff8 4*0 1c00 2c00 4000 41ec 43ec 3e00 1c00 7*0 1040 1080 1100 13ff 1c02 3082 d0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
  //   contents of rom_49 (hex, n*v repeats v):
  //   80 100 600 1fff e000 5*200 ffff 4*200 0 0 80 104 20e 414 824 3044 c084 304 c04 24 14 c 6 0 0 81 82
  //   84 feb8 9284 9282 9281 92ff 9291 9291 9291 fe91 91 81 81 0 1040 1080 9100 77ff 1900 c0 0 1ff8 1110
  //   1110 ffff 1110 1110 1ff8 4*0 1c00 2c00 4000 41ec 43ec 3e00 1c00 7*0 1040 1080 1100 13ff 1c02 3082
  //   d082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
  //   contents of rom_50 (hex, n*v repeats v):
  //   100 600 1fff e000 5*200 ffff 4*200 0 0 80 104 20e 414 824 3044 c084 304 c04 24 14 c 6 0 0 81 82 84
  //   feb8 9284 9282 9281 92ff 9291 9291 9291 fe91 91 81 81 0 1040 1080 9100 77ff 1900 c0 0 1ff8 1110 1110
  //   ffff 1110 1110 1ff8 4*0 1c00 2c00 4000 41ec 43ec 3e00 1c00 7*0 1040 1080 1100 13ff 1c02 3082 d082 10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
  //   contents of rom_51 (hex, n*v repeats v):
  //   600 1fff e000 5*200 ffff 4*200 0 0 80 104 20e 414 824 3044 c084 304 c04 24 14 c 6 0 0 81 82 84 feb8
  //   9284 9282 9281 92ff 9291 9291 9291 fe91 91 81 81 0 1040 1080 9100 77ff 1900 c0 0 1ff8 1110 1110 ffff
  //   1110 1110 1ff8 4*0 1c00 2c00 4000 41ec 43ec 3e00 1c00 7*0 1040 1080 1100 13ff 1c02 3082 d082 1082 1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
  //   contents of rom_52 (hex, n*v repeats v):
  //   1fff e000 5*200 ffff 4*200 0 0 80 104 20e 414 824 3044 c084 304 c04 24 14 c 6 0 0 81 82 84 feb8 9284
  //   9282 9281 92ff 9291 9291 9291 fe91 91 81 81 0 1040 1080 9100 77ff 1900 c0 0 1ff8 1110 1110 ffff 1110
  //   1110 1ff8 4*0 1c00 2c00 4000 41ec 43ec 3e00 1c00 7*0 1040 1080 1100 13ff 1c02 3082 d082 1082 1082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
  //   contents of rom_53 (hex, n*v repeats v):
  //   e000 5*200 ffff 4*200 0 0 80 104 20e 414 824 3044 c084 304 c04 24 14 c 6 0 0 81 82 84 feb8 9284 9282
  //   9281 92ff 9291 9291 9291 fe91 91 81 81 0 1040 1080 9100 77ff 1900 c0 0 1ff8 1110 1110 ffff 1110 1110
  //   1ff8 4*0 1c00 2c00 4000 41ec 43ec 3e00 1c00 7*0 1040 1080 1100 13ff 1c02 3082 d082 1082 1082 17fe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
  //   contents of rom_54 (hex, n*v repeats v):
  //   5*200 ffff 4*200 0 0 80 104 20e 414 824 3044 c084 304 c04 24 14 c 6 0 0 81 82 84 feb8 9284 9282 9281
  //   92ff 9291 9291 9291 fe91 91 81 81 0 1040 1080 9100 77ff 1900 c0 0 1ff8 1110 1110 ffff 1110 1110 1ff8
  //   4*0 1c00 2c00 4000 41ec 43ec 3e00 1c00 7*0 1040 1080 1100 13ff 1c02 3082 d082 1082 1082 17fe 4*108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
  //   contents of rom_55 (hex, n*v repeats v):
  //   4*200 ffff 4*200 0 0 80 104 20e 414 824 3044 c084 304 c04 24 14 c 6 0 0 81 82 84 feb8 9284 9282 9281
  //   92ff 9291 9291 9291 fe91 91 81 81 0 1040 1080 9100 77ff 1900 c0 0 1ff8 1110 1110 ffff 1110 1110 1ff8
  //   4*0 1c00 2c00 4000 41ec 43ec 3e00 1c00 7*0 1040 1080 1100 13ff 1c02 3082 d082 1082 1082 17fe 4*108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
  //   contents of rom_56 (hex, n*v repeats v):
  //   200 200 200 ffff 4*200 0 0 80 104 20e 414 824 3044 c084 304 c04 24 14 c 6 0 0 81 82 84 feb8 9284
  //   9282 9281 92ff 9291 9291 9291 fe91 91 81 81 0 1040 1080 9100 77ff 1900 c0 0 1ff8 1110 1110 ffff 1110
  //   1110 1ff8 4*0 1c00 2c00 4000 41ec 43ec 3e00 1c00 7*0 1040 1080 1100 13ff 1c02 3082 d082 1082 1082
  //   17fe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
  //   contents of rom_57 (hex, n*v repeats v):
  //   200 200 ffff 4*200 0 0 80 104 20e 414 824 3044 c084 304 c04 24 14 c 6 0 0 81 82 84 feb8 9284 9282
  //   9281 92ff 9291 9291 9291 fe91 91 81 81 0 1040 1080 9100 77ff 1900 c0 0 1ff8 1110 1110 ffff 1110 1110
  //   1ff8 4*0 1c00 2c00 4000 41ec 43ec 3e00 1c00 7*0 1040 1080 1100 13ff 1c02 3082 d082 1082 1082 17fe
  //   4*1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
  //   contents of rom_58 (hex, n*v repeats v):
  //   200 ffff 4*200 0 0 80 104 20e 414 824 3044 c084 304 c04 24 14 c 6 0 0 81 82 84 feb8 9284 9282 9281
  //   92ff 9291 9291 9291 fe91 91 81 81 0 1040 1080 9100 77ff 1900 c0 0 1ff8 1110 1110 ffff 1110 1110 1ff8
  //   4*0 1c00 2c00 4000 41ec 43ec 3e00 1c00 7*0 1040 1080 1100 13ff 1c02 3082 d082 1082 1082 17fe 4*1082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
  //   contents of rom_59 (hex, n*v repeats v):
  //   ffff 4*200 0 0 80 104 20e 414 824 3044 c084 304 c04 24 14 c 6 0 0 81 82 84 feb8 9284 9282 9281 92ff
  //   9291 9291 9291 fe91 91 81 81 0 1040 1080 9100 77ff 1900 c0 0 1ff8 1110 1110 ffff 1110 1110 1ff8 4*0
  //   1c00 2c00 4000 41ec 43ec 3e00 1c00 7*0 1040 1080 1100 13ff 1c02 3082 d082 1082 1082 17fe 4*1082 1002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
  //   contents of rom_60 (hex, n*v repeats v):
  //   4*200 0 0 80 104 20e 414 824 3044 c084 304 c04 24 14 c 6 0 0 81 82 84 feb8 9284 9282 9281 92ff 9291
  //   9291 9291 fe91 91 81 81 0 1040 1080 9100 77ff 1900 c0 0 1ff8 1110 1110 ffff 1110 1110 1ff8 4*0 1c00
  //   2c00 4000 41ec 43ec 3e00 1c00 7*0 1040 1080 1100 13ff 1c02 3082 d082 1082 1082 17fe 4*1082 1002 0 20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
  //   contents of rom_61 (hex, n*v repeats v):
  //   200 200 200 0 0 80 104 20e 414 824 3044 c084 304 c04 24 14 c 6 0 0 81 82 84 feb8 9284 9282 9281 92ff
  //   9291 9291 9291 fe91 91 81 81 0 1040 1080 9100 77ff 1900 c0 0 1ff8 1110 1110 ffff 1110 1110 1ff8 4*0
  //   1c00 2c00 4000 41ec 43ec 3e00 1c00 7*0 1040 1080 1100 13ff 1c02 3082 d082 1082 1082 17fe 4*1082 100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
  //   contents of rom_62 (hex, n*v repeats v):
  //   200 200 0 0 80 104 20e 414 824 3044 c084 304 c04 24 14 c 6 0 0 81 82 84 feb8 9284 9282 9281 92ff
  //   9291 9291 9291 fe91 91 81 81 0 1040 1080 9100 77ff 1900 c0 0 1ff8 1110 1110 ffff 1110 1110 1ff8 4*0
  //   1c00 2c00 4000 41ec 43ec 3e00 1c00 7*0 1040 1080 1100 13ff 1c02 3082 d082 1082 1082 17fe 4*1082 1002
  //   0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
  //   contents of rom_63 (hex, n*v repeats v):
  //   200 0 0 80 104 20e 414 824 3044 c084 304 c04 24 14 c 6 0 0 81 82 84 feb8 9284 9282 9281 92ff 9291
  //   9291 9291 fe91 91 81 81 0 1040 1080 9100 77ff 1900 c0 0 1ff8 1110 1110 ffff 1110 1110 1ff8 4*0 1c00
  //   2c00 4000 41ec 43ec 3e00 1c00 7*0 1040 1080 1100 13ff 1c02 3082 d082 1082 1082 17fe 4*1082 1002 0
  //   200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
  //   contents of rom_64 (hex, n*v repeats v):
  //   0 0 80 104 20e 414 824 3044 c084 304 c04 24 14 c 6 0 0 81 82 84 feb8 9284 9282 9281 92ff 9291 9291
  //   9291 fe91 91 81 81 0 1040 1080 9100 77ff 1900 c0 0 1ff8 1110 1110 ffff 1110 1110 1ff8 4*0 1c00 2c00
  //   4000 41ec 43ec 3e00 1c00 7*0 1040 1080 1100 13ff 1c02 3082 d082 1082 1082 17fe 4*1082 1002 0 200 200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
  //   contents of rom_65 (hex, n*v repeats v):
  //   0 80 104 20e 414 824 3044 c084 304 c04 24 14 c 6 0 0 81 82 84 feb8 9284 9282 9281 92ff 9291 9291
  //   9291 fe91 91 81 81 0 1040 1080 9100 77ff 1900 c0 0 1ff8 1110 1110 ffff 1110 1110 1ff8 4*0 1c00 2c00
  //   4000 41ec 43ec 3e00 1c00 7*0 1040 1080 1100 13ff 1c02 3082 d082 1082 1082 17fe 4*1082 1002 0 200 200
  //   42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
  //   contents of rom_66 (hex, n*v repeats v):
  //   80 104 20e 414 824 3044 c084 304 c04 24 14 c 6 0 0 81 82 84 feb8 9284 9282 9281 92ff 9291 9291 9291
  //   fe91 91 81 81 0 1040 1080 9100 77ff 1900 c0 0 1ff8 1110 1110 ffff 1110 1110 1ff8 4*0 1c00 2c00 4000
  //   41ec 43ec 3e00 1c00 7*0 1040 1080 1100 13ff 1c02 3082 d082 1082 1082 17fe 4*1082 1002 0 200 200 4200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
  //   contents of rom_67 (hex, n*v repeats v):
  //   104 20e 414 824 3044 c084 304 c04 24 14 c 6 0 0 81 82 84 feb8 9284 9282 9281 92ff 9291 9291 9291
  //   fe91 91 81 81 0 1040 1080 9100 77ff 1900 c0 0 1ff8 1110 1110 ffff 1110 1110 1ff8 4*0 1c00 2c00 4000
  //   41ec 43ec 3e00 1c00 7*0 1040 1080 1100 13ff 1c02 3082 d082 1082 1082 17fe 4*1082 1002 0 200 200 4200
  //   33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
  //   contents of rom_68 (hex, n*v repeats v):
  //   20e 414 824 3044 c084 304 c04 24 14 c 6 0 0 81 82 84 feb8 9284 9282 9281 92ff 9291 9291 9291 fe91 91
  //   81 81 0 1040 1080 9100 77ff 1900 c0 0 1ff8 1110 1110 ffff 1110 1110 1ff8 4*0 1c00 2c00 4000 41ec
  //   43ec 3e00 1c00 7*0 1040 1080 1100 13ff 1c02 3082 d082 1082 1082 17fe 4*1082 1002 0 200 200 4200 33fe
  //   4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
  //   contents of rom_69 (hex, n*v repeats v):
  //   414 824 3044 c084 304 c04 24 14 c 6 0 0 81 82 84 feb8 9284 9282 9281 92ff 9291 9291 9291 fe91 91 81
  //   81 0 1040 1080 9100 77ff 1900 c0 0 1ff8 1110 1110 ffff 1110 1110 1ff8 4*0 1c00 2c00 4000 41ec 43ec
  //   3e00 1c00 7*0 1040 1080 1100 13ff 1c02 3082 d082 1082 1082 17fe 4*1082 1002 0 200 200 4200 33fe 4 8
  //   8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
  //   contents of rom_70 (hex, n*v repeats v):
  //   824 3044 c084 304 c04 24 14 c 6 0 0 81 82 84 feb8 9284 9282 9281 92ff 9291 9291 9291 fe91 91 81 81 0
  //   1040 1080 9100 77ff 1900 c0 0 1ff8 1110 1110 ffff 1110 1110 1ff8 4*0 1c00 2c00 4000 41ec 43ec 3e00
  //   1c00 7*0 1040 1080 1100 13ff 1c02 3082 d082 1082 1082 17fe 4*1082 1002 0 200 200 4200 33fe 4 8 800 8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
  //   contents of rom_71 (hex, n*v repeats v):
  //   3044 c084 304 c04 24 14 c 6 0 0 81 82 84 feb8 9284 9282 9281 92ff 9291 9291 9291 fe91 91 81 81 0
  //   1040 1080 9100 77ff 1900 c0 0 1ff8 1110 1110 ffff 1110 1110 1ff8 4*0 1c00 2c00 4000 41ec 43ec 3e00
  //   1c00 7*0 1040 1080 1100 13ff 1c02 3082 d082 1082 1082 17fe 4*1082 1002 0 200 200 4200 33fe 4 8 800
  //   880 8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
  //   contents of rom_72 (hex, n*v repeats v):
  //   c084 304 c04 24 14 c 6 0 0 81 82 84 feb8 9284 9282 9281 92ff 9291 9291 9291 fe91 91 81 81 0 1040
  //   1080 9100 77ff 1900 c0 0 1ff8 1110 1110 ffff 1110 1110 1ff8 4*0 1c00 2c00 4000 41ec 43ec 3e00 1c00
  //   7*0 1040 1080 1100 13ff 1c02 3082 d082 1082 1082 17fe 4*1082 1002 0 200 200 4200 33fe 4 8 800 880
  //   860 80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
  //   contents of rom_73 (hex, n*v repeats v):
  //   304 c04 24 14 c 6 0 0 81 82 84 feb8 9284 9282 9281 92ff 9291 9291 9291 fe91 91 81 81 0 1040 1080
  //   9100 77ff 1900 c0 0 1ff8 1110 1110 ffff 1110 1110 1ff8 4*0 1c00 2c00 4000 41ec 43ec 3e00 1c00 7*0
  //   1040 1080 1100 13ff 1c02 3082 d082 1082 1082 17fe 4*1082 1002 0 200 200 4200 33fe 4 8 800 880 860
  //   802 801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
  //   contents of rom_74 (hex, n*v repeats v):
  //   c04 24 14 c 6 0 0 81 82 84 feb8 9284 9282 9281 92ff 9291 9291 9291 fe91 91 81 81 0 1040 1080 9100
  //   77ff 1900 c0 0 1ff8 1110 1110 ffff 1110 1110 1ff8 4*0 1c00 2c00 4000 41ec 43ec 3e00 1c00 7*0 1040
  //   1080 1100 13ff 1c02 3082 d082 1082 1082 17fe 4*1082 1002 0 200 200 4200 33fe 4 8 800 880 860 802 801
  //   fff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
  //   contents of rom_75 (hex, n*v repeats v):
  //   24 14 c 6 0 0 81 82 84 feb8 9284 9282 9281 92ff 9291 9291 9291 fe91 91 81 81 0 1040 1080 9100 77ff
  //   1900 c0 0 1ff8 1110 1110 ffff 1110 1110 1ff8 4*0 1c00 2c00 4000 41ec 43ec 3e00 1c00 7*0 1040 1080
  //   1100 13ff 1c02 3082 d082 1082 1082 17fe 4*1082 1002 0 200 200 4200 33fe 4 8 800 880 860 802 801 fffe
  //   80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
  //   contents of rom_76 (hex, n*v repeats v):
  //   14 c 6 0 0 81 82 84 feb8 9284 9282 9281 92ff 9291 9291 9291 fe91 91 81 81 0 1040 1080 9100 77ff 1900
  //   c0 0 1ff8 1110 1110 ffff 1110 1110 1ff8 4*0 1c00 2c00 4000 41ec 43ec 3e00 1c00 7*0 1040 1080 1100
  //   13ff 1c02 3082 d082 1082 1082 17fe 4*1082 1002 0 200 200 4200 33fe 4 8 800 880 860 802 801 fffe 800
  //   8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
  //   contents of rom_77 (hex, n*v repeats v):
  //   c 6 0 0 81 82 84 feb8 9284 9282 9281 92ff 9291 9291 9291 fe91 91 81 81 0 1040 1080 9100 77ff 1900 c0
  //   0 1ff8 1110 1110 ffff 1110 1110 1ff8 4*0 1c00 2c00 4000 41ec 43ec 3e00 1c00 7*0 1040 1080 1100 13ff
  //   1c02 3082 d082 1082 1082 17fe 4*1082 1002 0 200 200 4200 33fe 4 8 800 880 860 802 801 fffe 800 800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
  //   contents of rom_78 (hex, n*v repeats v):
  //   6 0 0 81 82 84 feb8 9284 9282 9281 92ff 9291 9291 9291 fe91 91 81 81 0 1040 1080 9100 77ff 1900 c0 0
  //   1ff8 1110 1110 ffff 1110 1110 1ff8 4*0 1c00 2c00 4000 41ec 43ec 3e00 1c00 7*0 1040 1080 1100 13ff
  //   1c02 3082 d082 1082 1082 17fe 4*1082 1002 0 200 200 4200 33fe 4 8 800 880 860 802 801 fffe 800 800
  //   80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
  //   contents of rom_79 (hex, n*v repeats v):
  //   0 0 81 82 84 feb8 9284 9282 9281 92ff 9291 9291 9291 fe91 91 81 81 0 1040 1080 9100 77ff 1900 c0 0
  //   1ff8 1110 1110 ffff 1110 1110 1ff8 4*0 1c00 2c00 4000 41ec 43ec 3e00 1c00 7*0 1040 1080 1100 13ff
  //   1c02 3082 d082 1082 1082 17fe 4*1082 1002 0 200 200 4200 33fe 4 8 800 880 860 802 801 fffe 800 800
  //   800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
  //   contents of rom_80 (hex, n*v repeats v):
  //   0 81 82 84 feb8 9284 9282 9281 92ff 9291 9291 9291 fe91 91 81 81 0 1040 1080 9100 77ff 1900 c0 0
  //   1ff8 1110 1110 ffff 1110 1110 1ff8 4*0 1c00 2c00 4000 41ec 43ec 3e00 1c00 7*0 1040 1080 1100 13ff
  //   1c02 3082 d082 1082 1082 17fe 4*1082 1002 0 200 200 4200 33fe 4 8 800 880 860 802 801 fffe 800 800
  //   800 0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
  //   contents of rom_81 (hex, n*v repeats v):
  //   81 82 84 feb8 9284 9282 9281 92ff 9291 9291 9291 fe91 91 81 81 0 1040 1080 9100 77ff 1900 c0 0 1ff8
  //   1110 1110 ffff 1110 1110 1ff8 4*0 1c00 2c00 4000 41ec 43ec 3e00 1c00 7*0 1040 1080 1100 13ff 1c02
  //   3082 d082 1082 1082 17fe 4*1082 1002 0 200 200 4200 33fe 4 8 800 880 860 802 801 fffe 800 800 800 0
  //   20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
  //   contents of rom_82 (hex, n*v repeats v):
  //   82 84 feb8 9284 9282 9281 92ff 9291 9291 9291 fe91 91 81 81 0 1040 1080 9100 77ff 1900 c0 0 1ff8
  //   1110 1110 ffff 1110 1110 1ff8 4*0 1c00 2c00 4000 41ec 43ec 3e00 1c00 7*0 1040 1080 1100 13ff 1c02
  //   3082 d082 1082 1082 17fe 4*1082 1002 0 200 200 4200 33fe 4 8 800 880 860 802 801 fffe 800 800 800 0
  //   200 2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
  //   contents of rom_83 (hex, n*v repeats v):
  //   84 feb8 9284 9282 9281 92ff 9291 9291 9291 fe91 91 81 81 0 1040 1080 9100 77ff 1900 c0 0 1ff8 1110
  //   1110 ffff 1110 1110 1ff8 4*0 1c00 2c00 4000 41ec 43ec 3e00 1c00 7*0 1040 1080 1100 13ff 1c02 3082
  //   d082 1082 1082 17fe 4*1082 1002 0 200 200 4200 33fe 4 8 800 880 860 802 801 fffe 800 800 800 0 200
  //   200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
  //   contents of rom_84 (hex, n*v repeats v):
  //   feb8 9284 9282 9281 92ff 9291 9291 9291 fe91 91 81 81 0 1040 1080 9100 77ff 1900 c0 0 1ff8 1110 1110
  //   ffff 1110 1110 1ff8 4*0 1c00 2c00 4000 41ec 43ec 3e00 1c00 7*0 1040 1080 1100 13ff 1c02 3082 d082
  //   1082 1082 17fe 4*1082 1002 0 200 200 4200 33fe 4 8 800 880 860 802 801 fffe 800 800 800 0 200 200
  //   420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
  //   contents of rom_85 (hex, n*v repeats v):
  //   9284 9282 9281 92ff 9291 9291 9291 fe91 91 81 81 0 1040 1080 9100 77ff 1900 c0 0 1ff8 1110 1110 ffff
  //   1110 1110 1ff8 4*0 1c00 2c00 4000 41ec 43ec 3e00 1c00 7*0 1040 1080 1100 13ff 1c02 3082 d082 1082
  //   1082 17fe 4*1082 1002 0 200 200 4200 33fe 4 8 800 880 860 802 801 fffe 800 800 800 0 200 200 4200
  //   33f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
  //   contents of rom_86 (hex, n*v repeats v):
  //   9282 9281 92ff 9291 9291 9291 fe91 91 81 81 0 1040 1080 9100 77ff 1900 c0 0 1ff8 1110 1110 ffff 1110
  //   1110 1ff8 4*0 1c00 2c00 4000 41ec 43ec 3e00 1c00 7*0 1040 1080 1100 13ff 1c02 3082 d082 1082 1082
  //   17fe 4*1082 1002 0 200 200 4200 33fe 4 8 800 880 860 802 801 fffe 800 800 800 0 200 200 4200 33fe 4
  //   2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
  //   contents of rom_87 (hex, n*v repeats v):
  //   9281 92ff 9291 9291 9291 fe91 91 81 81 0 1040 1080 9100 77ff 1900 c0 0 1ff8 1110 1110 ffff 1110 1110
  //   1ff8 4*0 1c00 2c00 4000 41ec 43ec 3e00 1c00 7*0 1040 1080 1100 13ff 1c02 3082 d082 1082 1082 17fe
  //   4*1082 1002 0 200 200 4200 33fe 4 8 800 880 860 802 801 fffe 800 800 800 0 200 200 4200 33fe 4 208
  //   40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
  //   contents of rom_88 (hex, n*v repeats v):
  //   92ff 9291 9291 9291 fe91 91 81 81 0 1040 1080 9100 77ff 1900 c0 0 1ff8 1110 1110 ffff 1110 1110 1ff8
  //   4*0 1c00 2c00 4000 41ec 43ec 3e00 1c00 7*0 1040 1080 1100 13ff 1c02 3082 d082 1082 1082 17fe 4*1082
  //   1002 0 200 200 4200 33fe 4 8 800 880 860 802 801 fffe 800 800 800 0 200 200 4200 33fe 4 208 400 9fc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
  //   contents of rom_89 (hex, n*v repeats v):
  //   9291 9291 9291 fe91 91 81 81 0 1040 1080 9100 77ff 1900 c0 0 1ff8 1110 1110 ffff 1110 1110 1ff8 4*0
  //   1c00 2c00 4000 41ec 43ec 3e00 1c00 7*0 1040 1080 1100 13ff 1c02 3082 d082 1082 1082 17fe 4*1082 1002
  //   0 200 200 4200 33fe 4 8 800 880 860 802 801 fffe 800 800 800 0 200 200 4200 33fe 4 208 400 9fc 3022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
  //   contents of rom_90 (hex, n*v repeats v):
  //   9291 9291 fe91 91 81 81 0 1040 1080 9100 77ff 1900 c0 0 1ff8 1110 1110 ffff 1110 1110 1ff8 4*0 1c00
  //   2c00 4000 41ec 43ec 3e00 1c00 7*0 1040 1080 1100 13ff 1c02 3082 d082 1082 1082 17fe 4*1082 1002 0
  //   200 200 4200 33fe 4 8 800 880 860 802 801 fffe 800 800 800 0 200 200 4200 33fe 4 208 400 9fc 3022
  //   c042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
  //   contents of rom_91 (hex, n*v repeats v):
  //   9291 fe91 91 81 81 0 1040 1080 9100 77ff 1900 c0 0 1ff8 1110 1110 ffff 1110 1110 1ff8 4*0 1c00 2c00
  //   4000 41ec 43ec 3e00 1c00 7*0 1040 1080 1100 13ff 1c02 3082 d082 1082 1082 17fe 4*1082 1002 0 200 200
  //   4200 33fe 4 8 800 880 860 802 801 fffe 800 800 800 0 200 200 4200 33fe 4 208 400 9fc 3022 c042 3082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
  //   contents of rom_92 (hex, n*v repeats v):
  //   fe91 91 81 81 0 1040 1080 9100 77ff 1900 c0 0 1ff8 1110 1110 ffff 1110 1110 1ff8 4*0 1c00 2c00 4000
  //   41ec 43ec 3e00 1c00 7*0 1040 1080 1100 13ff 1c02 3082 d082 1082 1082 17fe 4*1082 1002 0 200 200 4200
  //   33fe 4 8 800 880 860 802 801 fffe 800 800 800 0 200 200 4200 33fe 4 208 400 9fc 3022 c042 3082 902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
  //   contents of rom_93 (hex, n*v repeats v):
  //   91 81 81 0 1040 1080 9100 77ff 1900 c0 0 1ff8 1110 1110 ffff 1110 1110 1ff8 4*0 1c00 2c00 4000 41ec
  //   43ec 3e00 1c00 7*0 1040 1080 1100 13ff 1c02 3082 d082 1082 1082 17fe 4*1082 1002 0 200 200 4200 33fe
  //   4 8 800 880 860 802 801 fffe 800 800 800 0 200 200 4200 33fe 4 208 400 9fc 3022 c042 3082 902 402 2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
  //   contents of rom_94 (hex, n*v repeats v):
  //   81 81 0 1040 1080 9100 77ff 1900 c0 0 1ff8 1110 1110 ffff 1110 1110 1ff8 4*0 1c00 2c00 4000 41ec
  //   43ec 3e00 1c00 7*0 1040 1080 1100 13ff 1c02 3082 d082 1082 1082 17fe 4*1082 1002 0 200 200 4200 33fe
  //   4 8 800 880 860 802 801 fffe 800 800 800 0 200 200 4200 33fe 4 208 400 9fc 3022 c042 3082 902 402
  //   20e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
  //   contents of rom_95 (hex, n*v repeats v):
  //   81 0 1040 1080 9100 77ff 1900 c0 0 1ff8 1110 1110 ffff 1110 1110 1ff8 4*0 1c00 2c00 4000 41ec 43ec
  //   3e00 1c00 7*0 1040 1080 1100 13ff 1c02 3082 d082 1082 1082 17fe 4*1082 1002 0 200 200 4200 33fe 4 8
  //   800 880 860 802 801 fffe 800 800 800 0 200 200 4200 33fe 4 208 400 9fc 3022 c042 3082 902 402 20e
  //   200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
  //   contents of rom_96 (hex, n*v repeats v):
  //   0 1040 1080 9100 77ff 1900 c0 0 1ff8 1110 1110 ffff 1110 1110 1ff8 4*0 1c00 2c00 4000 41ec 43ec 3e00
  //   1c00 7*0 1040 1080 1100 13ff 1c02 3082 d082 1082 1082 17fe 4*1082 1002 0 200 200 4200 33fe 4 8 800
  //   880 860 802 801 fffe 800 800 800 0 200 200 4200 33fe 4 208 400 9fc 3022 c042 3082 902 402 20e 200 0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
  //   contents of rom_97 (hex, n*v repeats v):
  //   1040 1080 9100 77ff 1900 c0 0 1ff8 1110 1110 ffff 1110 1110 1ff8 4*0 1c00 2c00 4000 41ec 43ec 3e00
  //   1c00 7*0 1040 1080 1100 13ff 1c02 3082 d082 1082 1082 17fe 4*1082 1002 0 200 200 4200 33fe 4 8 800
  //   880 860 802 801 fffe 800 800 800 0 200 200 4200 33fe 4 208 400 9fc 3022 c042 3082 902 402 20e 200 0
  //   20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
  //   contents of rom_98 (hex, n*v repeats v):
  //   1080 9100 77ff 1900 c0 0 1ff8 1110 1110 ffff 1110 1110 1ff8 4*0 1c00 2c00 4000 41ec 43ec 3e00 1c00
  //   7*0 1040 1080 1100 13ff 1c02 3082 d082 1082 1082 17fe 4*1082 1002 0 200 200 4200 33fe 4 8 800 880
  //   860 802 801 fffe 800 800 800 0 200 200 4200 33fe 4 208 400 9fc 3022 c042 3082 902 402 20e 200 0 200
  //   202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
  //   contents of rom_99 (hex, n*v repeats v):
  //   9100 77ff 1900 c0 0 1ff8 1110 1110 ffff 1110 1110 1ff8 4*0 1c00 2c00 4000 41ec 43ec 3e00 1c00 7*0
  //   1040 1080 1100 13ff 1c02 3082 d082 1082 1082 17fe 4*1082 1002 0 200 200 4200 33fe 4 8 800 880 860
  //   802 801 fffe 800 800 800 0 200 200 4200 33fe 4 208 400 9fc 3022 c042 3082 902 402 20e 200 0 200 202
  //   4204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
  //   contents of rom_100 (hex, n*v repeats v):
  //   77ff 1900 c0 0 1ff8 1110 1110 ffff 1110 1110 1ff8 4*0 1c00 2c00 4000 41ec 43ec 3e00 1c00 7*0 1040
  //   1080 1100 13ff 1c02 3082 d082 1082 1082 17fe 4*1082 1002 0 200 200 4200 33fe 4 8 800 880 860 802 801
  //   fffe 800 800 800 0 200 200 4200 33fe 4 208 400 9fc 3022 c042 3082 902 402 20e 200 0 200 202 4204
  //   33f8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
  //   contents of rom_101 (hex, n*v repeats v):
  //   1900 c0 0 1ff8 1110 1110 ffff 1110 1110 1ff8 4*0 1c00 2c00 4000 41ec 43ec 3e00 1c00 7*0 1040 1080
  //   1100 13ff 1c02 3082 d082 1082 1082 17fe 4*1082 1002 0 200 200 4200 33fe 4 8 800 880 860 802 801 fffe
  //   800 800 800 0 200 200 4200 33fe 4 208 400 9fc 3022 c042 3082 902 402 20e 200 0 200 202 4204 33f8 4
  //   10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
  //   contents of rom_102 (hex, n*v repeats v):
  //   c0 0 1ff8 1110 1110 ffff 1110 1110 1ff8 4*0 1c00 2c00 4000 41ec 43ec 3e00 1c00 7*0 1040 1080 1100
  //   13ff 1c02 3082 d082 1082 1082 17fe 4*1082 1002 0 200 200 4200 33fe 4 8 800 880 860 802 801 fffe 800
  //   800 800 0 200 200 4200 33fe 4 208 400 9fc 3022 c042 3082 902 402 20e 200 0 200 202 4204 33f8 4 100a
  //   14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
  //   contents of rom_103 (hex, n*v repeats v):
  //   0 1ff8 1110 1110 ffff 1110 1110 1ff8 4*0 1c00 2c00 4000 41ec 43ec 3e00 1c00 7*0 1040 1080 1100 13ff
  //   1c02 3082 d082 1082 1082 17fe 4*1082 1002 0 200 200 4200 33fe 4 8 800 880 860 802 801 fffe 800 800
  //   800 0 200 200 4200 33fe 4 208 400 9fc 3022 c042 3082 902 402 20e 200 0 200 202 4204 33f8 4 100a 1412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
  //   contents of rom_104 (hex, n*v repeats v):
  //   1ff8 1110 1110 ffff 1110 1110 1ff8 4*0 1c00 2c00 4000 41ec 43ec 3e00 1c00 7*0 1040 1080 1100 13ff
  //   1c02 3082 d082 1082 1082 17fe 4*1082 1002 0 200 200 4200 33fe 4 8 800 880 860 802 801 fffe 800 800
  //   800 0 200 200 4200 33fe 4 208 400 9fc 3022 c042 3082 902 402 20e 200 0 200 202 4204 33f8 4 100a 1412
  //   12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
  //   contents of rom_105 (hex, n*v repeats v):
  //   1110 1110 ffff 1110 1110 1ff8 4*0 1c00 2c00 4000 41ec 43ec 3e00 1c00 7*0 1040 1080 1100 13ff 1c02
  //   3082 d082 1082 1082 17fe 4*1082 1002 0 200 200 4200 33fe 4 8 800 880 860 802 801 fffe 800 800 800 0
  //   200 200 4200 33fe 4 208 400 9fc 3022 c042 3082 902 402 20e 200 0 200 202 4204 33f8 4 100a 1412 1222
  //   91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
  //   contents of rom_106 (hex, n*v repeats v):
  //   1110 ffff 1110 1110 1ff8 4*0 1c00 2c00 4000 41ec 43ec 3e00 1c00 7*0 1040 1080 1100 13ff 1c02 3082
  //   d082 1082 1082 17fe 4*1082 1002 0 200 200 4200 33fe 4 8 800 880 860 802 801 fffe 800 800 800 0 200
  //   200 4200 33fe 4 208 400 9fc 3022 c042 3082 902 402 20e 200 0 200 202 4204 33f8 4 100a 1412 1222 9142
  //   70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
  //   contents of rom_107 (hex, n*v repeats v):
  //   ffff 1110 1110 1ff8 4*0 1c00 2c00 4000 41ec 43ec 3e00 1c00 7*0 1040 1080 1100 13ff 1c02 3082 d082
  //   1082 1082 17fe 4*1082 1002 0 200 200 4200 33fe 4 8 800 880 860 802 801 fffe 800 800 800 0 200 200
  //   4200 33fe 4 208 400 9fc 3022 c042 3082 902 402 20e 200 0 200 202 4204 33f8 4 100a 1412 1222 9142
  //   7082 13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
  //   contents of rom_108 (hex, n*v repeats v):
  //   1110 1110 1ff8 4*0 1c00 2c00 4000 41ec 43ec 3e00 1c00 7*0 1040 1080 1100 13ff 1c02 3082 d082 1082
  //   1082 17fe 4*1082 1002 0 200 200 4200 33fe 4 8 800 880 860 802 801 fffe 800 800 800 0 200 200 4200
  //   33fe 4 208 400 9fc 3022 c042 3082 902 402 20e 200 0 200 202 4204 33f8 4 100a 1412 1222 9142 7082
  //   1342 1c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
  //   contents of rom_109 (hex, n*v repeats v):
  //   1110 1ff8 4*0 1c00 2c00 4000 41ec 43ec 3e00 1c00 7*0 1040 1080 1100 13ff 1c02 3082 d082 1082 1082
  //   17fe 4*1082 1002 0 200 200 4200 33fe 4 8 800 880 860 802 801 fffe 800 800 800 0 200 200 4200 33fe 4
  //   208 400 9fc 3022 c042 3082 902 402 20e 200 0 200 202 4204 33f8 4 100a 1412 1222 9142 7082 1342 1c22
  //   10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
  //   contents of rom_110 (hex, n*v repeats v):
  //   1ff8 4*0 1c00 2c00 4000 41ec 43ec 3e00 1c00 7*0 1040 1080 1100 13ff 1c02 3082 d082 1082 1082 17fe
  //   4*1082 1002 0 200 200 4200 33fe 4 8 800 880 860 802 801 fffe 800 800 800 0 200 200 4200 33fe 4 208
  //   400 9fc 3022 c042 3082 902 402 20e 200 0 200 202 4204 33f8 4 100a 1412 1222 9142 7082 1342 1c22 101a
  //   10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
  //   contents of rom_111 (hex, n*v repeats v):
  //   4*0 1c00 2c00 4000 41ec 43ec 3e00 1c00 7*0 1040 1080 1100 13ff 1c02 3082 d082 1082 1082 17fe 4*1082
  //   1002 0 200 200 4200 33fe 4 8 800 880 860 802 801 fffe 800 800 800 0 200 200 4200 33fe 4 208 400 9fc
  //   3022 c042 3082 902 402 20e 200 0 200 202 4204 33f8 4 100a 1412 1222 9142 7082 1342 1c22 101a 1002 2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
  //   contents of rom_112 (hex, n*v repeats v):
  //   0 0 0 1c00 2c00 4000 41ec 43ec 3e00 1c00 7*0 1040 1080 1100 13ff 1c02 3082 d082 1082 1082 17fe
  //   4*1082 1002 0 200 200 4200 33fe 4 8 800 880 860 802 801 fffe 800 800 800 0 200 200 4200 33fe 4 208
  //   400 9fc 3022 c042 3082 902 402 20e 200 0 200 202 4204 33f8 4 100a 1412 1222 9142 7082 1342 1c22 101a
  //   1002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
  //   contents of rom_113 (hex, n*v repeats v):
  //   0 0 1c00 2c00 4000 41ec 43ec 3e00 1c00 7*0 1040 1080 1100 13ff 1c02 3082 d082 1082 1082 17fe 4*1082
  //   1002 0 200 200 4200 33fe 4 8 800 880 860 802 801 fffe 800 800 800 0 200 200 4200 33fe 4 208 400 9fc
  //   3022 c042 3082 902 402 20e 200 0 200 202 4204 33f8 4 100a 1412 1222 9142 7082 1342 1c22 101a 1002 2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
  //   contents of rom_114 (hex, n*v repeats v):
  //   0 1c00 2c00 4000 41ec 43ec 3e00 1c00 7*0 1040 1080 1100 13ff 1c02 3082 d082 1082 1082 17fe 4*1082
  //   1002 0 200 200 4200 33fe 4 8 800 880 860 802 801 fffe 800 800 800 0 200 200 4200 33fe 4 208 400 9fc
  //   3022 c042 3082 902 402 20e 200 0 200 202 4204 33f8 4 100a 1412 1222 9142 7082 1342 1c22 101a 1002 2
  //   0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
  //   contents of rom_115 (hex, n*v repeats v):
  //   1c00 2c00 4000 41ec 43ec 3e00 1c00 7*0 1040 1080 1100 13ff 1c02 3082 d082 1082 1082 17fe 4*1082 1002
  //   0 200 200 4200 33fe 4 8 800 880 860 802 801 fffe 800 800 800 0 200 200 4200 33fe 4 208 400 9fc 3022
  //   c042 3082 902 402 20e 200 0 200 202 4204 33f8 4 100a 1412 1222 9142 7082 1342 1c22 101a 1002 2 0 10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
  //   contents of rom_116 (hex, n*v repeats v):
  //   2c00 4000 41ec 43ec 3e00 1c00 7*0 1040 1080 1100 13ff 1c02 3082 d082 1082 1082 17fe 4*1082 1002 0
  //   200 200 4200 33fe 4 8 800 880 860 802 801 fffe 800 800 800 0 200 200 4200 33fe 4 208 400 9fc 3022
  //   c042 3082 902 402 20e 200 0 200 202 4204 33f8 4 100a 1412 1222 9142 7082 1342 1c22 101a 1002 2 0 100
  //   100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
  //   contents of rom_117 (hex, n*v repeats v):
  //   4000 41ec 43ec 3e00 1c00 7*0 1040 1080 1100 13ff 1c02 3082 d082 1082 1082 17fe 4*1082 1002 0 200 200
  //   4200 33fe 4 8 800 880 860 802 801 fffe 800 800 800 0 200 200 4200 33fe 4 208 400 9fc 3022 c042 3082
  //   902 402 20e 200 0 200 202 4204 33f8 4 100a 1412 1222 9142 7082 1342 1c22 101a 1002 2 0 100 100 200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
  //   contents of rom_118 (hex, n*v repeats v):
  //   41ec 43ec 3e00 1c00 7*0 1040 1080 1100 13ff 1c02 3082 d082 1082 1082 17fe 4*1082 1002 0 200 200 4200
  //   33fe 4 8 800 880 860 802 801 fffe 800 800 800 0 200 200 4200 33fe 4 208 400 9fc 3022 c042 3082 902
  //   402 20e 200 0 200 202 4204 33f8 4 100a 1412 1222 9142 7082 1342 1c22 101a 1002 2 0 100 100 200 400 8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
  //   contents of rom_119 (hex, n*v repeats v):
  //   43ec 3e00 1c00 7*0 1040 1080 1100 13ff 1c02 3082 d082 1082 1082 17fe 4*1082 1002 0 200 200 4200 33fe
  //   4 8 800 880 860 802 801 fffe 800 800 800 0 200 200 4200 33fe 4 208 400 9fc 3022 c042 3082 902 402
  //   20e 200 0 200 202 4204 33f8 4 100a 1412 1222 9142 7082 1342 1c22 101a 1002 2 0 100 100 200 400 800
  //   10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
  //   contents of rom_120 (hex, n*v repeats v):
  //   3e00 1c00 7*0 1040 1080 1100 13ff 1c02 3082 d082 1082 1082 17fe 4*1082 1002 0 200 200 4200 33fe 4 8
  //   800 880 860 802 801 fffe 800 800 800 0 200 200 4200 33fe 4 208 400 9fc 3022 c042 3082 902 402 20e
  //   200 0 200 202 4204 33f8 4 100a 1412 1222 9142 7082 1342 1c22 101a 1002 2 0 100 100 200 400 800 1000
  //   20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
  //   contents of rom_121 (hex, n*v repeats v):
  //   1c00 7*0 1040 1080 1100 13ff 1c02 3082 d082 1082 1082 17fe 4*1082 1002 0 200 200 4200 33fe 4 8 800
  //   880 860 802 801 fffe 800 800 800 0 200 200 4200 33fe 4 208 400 9fc 3022 c042 3082 902 402 20e 200 0
  //   200 202 4204 33f8 4 100a 1412 1222 9142 7082 1342 1c22 101a 1002 2 0 100 100 200 400 800 1000 2000
  //   c3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
  //   contents of rom_122 (hex, n*v repeats v):
  //   7*0 1040 1080 1100 13ff 1c02 3082 d082 1082 1082 17fe 4*1082 1002 0 200 200 4200 33fe 4 8 800 880
  //   860 802 801 fffe 800 800 800 0 200 200 4200 33fe 4 208 400 9fc 3022 c042 3082 902 402 20e 200 0 200
  //   202 4204 33f8 4 100a 1412 1222 9142 7082 1342 1c22 101a 1002 2 0 100 100 200 400 800 1000 2000 c3ff
  //   20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
  //   contents of rom_123 (hex, n*v repeats v):
  //   6*0 1040 1080 1100 13ff 1c02 3082 d082 1082 1082 17fe 4*1082 1002 0 200 200 4200 33fe 4 8 800 880
  //   860 802 801 fffe 800 800 800 0 200 200 4200 33fe 4 208 400 9fc 3022 c042 3082 902 402 20e 200 0 200
  //   202 4204 33f8 4 100a 1412 1222 9142 7082 1342 1c22 101a 1002 2 0 100 100 200 400 800 1000 2000 c3ff
  //   20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
  //   contents of rom_124 (hex, n*v repeats v):
  //   5*0 1040 1080 1100 13ff 1c02 3082 d082 1082 1082 17fe 4*1082 1002 0 200 200 4200 33fe 4 8 800 880
  //   860 802 801 fffe 800 800 800 0 200 200 4200 33fe 4 208 400 9fc 3022 c042 3082 902 402 20e 200 0 200
  //   202 4204 33f8 4 100a 1412 1222 9142 7082 1342 1c22 101a 1002 2 0 100 100 200 400 800 1000 2000 c3ff
  //   20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
  //   contents of rom_125 (hex, n*v repeats v):
  //   4*0 1040 1080 1100 13ff 1c02 3082 d082 1082 1082 17fe 4*1082 1002 0 200 200 4200 33fe 4 8 800 880
  //   860 802 801 fffe 800 800 800 0 200 200 4200 33fe 4 208 400 9fc 3022 c042 3082 902 402 20e 200 0 200
  //   202 4204 33f8 4 100a 1412 1222 9142 7082 1342 1c22 101a 1002 2 0 100 100 200 400 800 1000 2000 c3ff
  //   20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
  //   contents of rom_126 (hex, n*v repeats v):
  //   0 0 0 1040 1080 1100 13ff 1c02 3082 d082 1082 1082 17fe 4*1082 1002 0 200 200 4200 33fe 4 8 800 880
  //   860 802 801 fffe 800 800 800 0 200 200 4200 33fe 4 208 400 9fc 3022 c042 3082 902 402 20e 200 0 200
  //   202 4204 33f8 4 100a 1412 1222 9142 7082 1342 1c22 101a 1002 2 0 100 100 200 400 800 1000 2000 c3ff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
  //   contents of rom_127 (hex, n*v repeats v):
  //   0 0 1040 1080 1100 13ff 1c02 3082 d082 1082 1082 17fe 4*1082 1002 0 200 200 4200 33fe 4 8 800 880
  //   860 802 801 fffe 800 800 800 0 200 200 4200 33fe 4 208 400 9fc 3022 c042 3082 902 402 20e 200 0 200
  //   202 4204 33f8 4 100a 1412 1222 9142 7082 1342 1c22 101a 1002 2 0 100 100 200 400 800 1000 2000 c3ff
  //   20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
  //   contents of rom_128 (hex, n*v repeats v):
  //   0 1040 1080 1100 13ff 1c02 3082 d082 1082 1082 17fe 4*1082 1002 0 200 200 4200 33fe 4 8 800 880 860
  //   802 801 fffe 800 800 800 0 200 200 4200 33fe 4 208 400 9fc 3022 c042 3082 902 402 20e 200 0 200 202
  //   4204 33f8 4 100a 1412 1222 9142 7082 1342 1c22 101a 1002 2 0 100 100 200 400 800 1000 2000 c3ff 2000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
  //   contents of rom_129 (hex, n*v repeats v):
  //   1040 1080 1100 13ff 1c02 3082 d082 1082 1082 17fe 4*1082 1002 0 200 200 4200 33fe 4 8 800 880 860
  //   802 801 fffe 800 800 800 0 200 200 4200 33fe 4 208 400 9fc 3022 c042 3082 902 402 20e 200 0 200 202
  //   4204 33f8 4 100a 1412 1222 9142 7082 1342 1c22 101a 1002 2 0 100 100 200 400 800 1000 2000 c3ff 2000
  //   1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
  //   contents of rom_130 (hex, n*v repeats v):
  //   1080 1100 13ff 1c02 3082 d082 1082 1082 17fe 4*1082 1002 0 200 200 4200 33fe 4 8 800 880 860 802 801
  //   fffe 800 800 800 0 200 200 4200 33fe 4 208 400 9fc 3022 c042 3082 902 402 20e 200 0 200 202 4204
  //   33f8 4 100a 1412 1222 9142 7082 1342 1c22 101a 1002 2 0 100 100 200 400 800 1000 2000 c3ff 2000 1000
  //   8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
  //   contents of rom_131 (hex, n*v repeats v):
  //   1100 13ff 1c02 3082 d082 1082 1082 17fe 4*1082 1002 0 200 200 4200 33fe 4 8 800 880 860 802 801 fffe
  //   800 800 800 0 200 200 4200 33fe 4 208 400 9fc 3022 c042 3082 902 402 20e 200 0 200 202 4204 33f8 4
  //   100a 1412 1222 9142 7082 1342 1c22 101a 1002 2 0 100 100 200 400 800 1000 2000 c3ff 2000 1000 800 40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
  //   contents of rom_132 (hex, n*v repeats v):
  //   13ff 1c02 3082 d082 1082 1082 17fe 4*1082 1002 0 200 200 4200 33fe 4 8 800 880 860 802 801 fffe 800
  //   800 800 0 200 200 4200 33fe 4 208 400 9fc 3022 c042 3082 902 402 20e 200 0 200 202 4204 33f8 4 100a
  //   1412 1222 9142 7082 1342 1c22 101a 1002 2 0 100 100 200 400 800 1000 2000 c3ff 2000 1000 800 400 200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
  //   contents of rom_133 (hex, n*v repeats v):
  //   1c02 3082 d082 1082 1082 17fe 4*1082 1002 0 200 200 4200 33fe 4 8 800 880 860 802 801 fffe 800 800
  //   800 0 200 200 4200 33fe 4 208 400 9fc 3022 c042 3082 902 402 20e 200 0 200 202 4204 33f8 4 100a 1412
  //   1222 9142 7082 1342 1c22 101a 1002 2 0 100 100 200 400 800 1000 2000 c3ff 2000 1000 800 400 200 100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
  //   contents of rom_134 (hex, n*v repeats v):
  //   3082 d082 1082 1082 17fe 4*1082 1002 0 200 200 4200 33fe 4 8 800 880 860 802 801 fffe 800 800 800 0
  //   200 200 4200 33fe 4 208 400 9fc 3022 c042 3082 902 402 20e 200 0 200 202 4204 33f8 4 100a 1412 1222
  //   9142 7082 1342 1c22 101a 1002 2 0 100 100 200 400 800 1000 2000 c3ff 2000 1000 800 400 200 100 100 0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
  //   contents of rom_135 (hex, n*v repeats v):
  //   d082 1082 1082 17fe 4*1082 1002 0 200 200 4200 33fe 4 8 800 880 860 802 801 fffe 800 800 800 0 200
  //   200 4200 33fe 4 208 400 9fc 3022 c042 3082 902 402 20e 200 0 200 202 4204 33f8 4 100a 1412 1222 9142
  //   7082 1342 1c22 101a 1002 2 0 100 100 200 400 800 1000 2000 c3ff 2000 1000 800 400 200 100 100 0 0 1f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
  //   contents of rom_136 (hex, n*v repeats v):
  //   1082 1082 17fe 4*1082 1002 0 200 200 4200 33fe 4 8 800 880 860 802 801 fffe 800 800 800 0 200 200
  //   4200 33fe 4 208 400 9fc 3022 c042 3082 902 402 20e 200 0 200 202 4204 33f8 4 100a 1412 1222 9142
  //   7082 1342 1c22 101a 1002 2 0 100 100 200 400 800 1000 2000 c3ff 2000 1000 800 400 200 100 100 0 0
  //   1fff 80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
  //   contents of rom_137 (hex, n*v repeats v):
  //   1082 17fe 4*1082 1002 0 200 200 4200 33fe 4 8 800 880 860 802 801 fffe 800 800 800 0 200 200 4200
  //   33fe 4 208 400 9fc 3022 c042 3082 902 402 20e 200 0 200 202 4204 33f8 4 100a 1412 1222 9142 7082
  //   1342 1c22 101a 1002 2 0 100 100 200 400 800 1000 2000 c3ff 2000 1000 800 400 200 100 100 0 0 1fff
  //   8000 40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
  //   contents of rom_138 (hex, n*v repeats v):
  //   17fe 4*1082 1002 0 200 200 4200 33fe 4 8 800 880 860 802 801 fffe 800 800 800 0 200 200 4200 33fe 4
  //   208 400 9fc 3022 c042 3082 902 402 20e 200 0 200 202 4204 33f8 4 100a 1412 1222 9142 7082 1342 1c22
  //   101a 1002 2 0 100 100 200 400 800 1000 2000 c3ff 2000 1000 800 400 200 100 100 0 0 1fff 8000 4000 0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
  //   contents of rom_139 (hex, n*v repeats v):
  //   4*1082 1002 0 200 200 4200 33fe 4 8 800 880 860 802 801 fffe 800 800 800 0 200 200 4200 33fe 4 208
  //   400 9fc 3022 c042 3082 902 402 20e 200 0 200 202 4204 33f8 4 100a 1412 1222 9142 7082 1342 1c22 101a
  //   1002 2 0 100 100 200 400 800 1000 2000 c3ff 2000 1000 800 400 200 100 100 0 0 1fff 8000 4000 0 47f8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
  //   contents of rom_140 (hex, n*v repeats v):
  //   1082 1082 1082 1002 0 200 200 4200 33fe 4 8 800 880 860 802 801 fffe 800 800 800 0 200 200 4200 33fe
  //   4 208 400 9fc 3022 c042 3082 902 402 20e 200 0 200 202 4204 33f8 4 100a 1412 1222 9142 7082 1342
  //   1c22 101a 1002 2 0 100 100 200 400 800 1000 2000 c3ff 2000 1000 800 400 200 100 100 0 0 1fff 8000
  //   4000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
  //   contents of rom_141 (hex, n*v repeats v):
  //   1082 1082 1002 0 200 200 4200 33fe 4 8 800 880 860 802 801 fffe 800 800 800 0 200 200 4200 33fe 4
  //   208 400 9fc 3022 c042 3082 902 402 20e 200 0 200 202 4204 33f8 4 100a 1412 1222 9142 7082 1342 1c22
  //   101a 1002 2 0 100 100 200 400 800 1000 2000 c3ff 2000 1000 800 400 200 100 100 0 0 1fff 8000 4000 0
  //   47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
  //   contents of rom_142 (hex, n*v repeats v):
  //   1082 1002 0 200 200 4200 33fe 4 8 800 880 860 802 801 fffe 800 800 800 0 200 200 4200 33fe 4 208 400
  //   9fc 3022 c042 3082 902 402 20e 200 0 200 202 4204 33f8 4 100a 1412 1222 9142 7082 1342 1c22 101a
  //   1002 2 0 100 100 200 400 800 1000 2000 c3ff 2000 1000 800 400 200 100 100 0 0 1fff 8000 4000 0 47f8
  //   44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
  //   contents of rom_143 (hex, n*v repeats v):
  //   1002 0 200 200 4200 33fe 4 8 800 880 860 802 801 fffe 800 800 800 0 200 200 4200 33fe 4 208 400 9fc
  //   3022 c042 3082 902 402 20e 200 0 200 202 4204 33f8 4 100a 1412 1222 9142 7082 1342 1c22 101a 1002 2
  //   0 100 100 200 400 800 1000 2000 c3ff 2000 1000 800 400 200 100 100 0 0 1fff 8000 4000 0 47f8 4410 44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
  //   contents of rom_144 (hex, n*v repeats v):
  //   0 200 200 4200 33fe 4 8 800 880 860 802 801 fffe 800 800 800 0 200 200 4200 33fe 4 208 400 9fc 3022
  //   c042 3082 902 402 20e 200 0 200 202 4204 33f8 4 100a 1412 1222 9142 7082 1342 1c22 101a 1002 2 0 100
  //   100 200 400 800 1000 2000 c3ff 2000 1000 800 400 200 100 100 0 0 1fff 8000 4000 0 47f8 4410 4410 44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
  //   contents of rom_145 (hex, n*v repeats v):
  //   200 200 4200 33fe 4 8 800 880 860 802 801 fffe 800 800 800 0 200 200 4200 33fe 4 208 400 9fc 3022
  //   c042 3082 902 402 20e 200 0 200 202 4204 33f8 4 100a 1412 1222 9142 7082 1342 1c22 101a 1002 2 0 100
  //   100 200 400 800 1000 2000 c3ff 2000 1000 800 400 200 100 100 0 0 1fff 8000 4000 0 47f8 4410 4410
  //   4410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
  //   contents of rom_146 (hex, n*v repeats v):
  //   200 4200 33fe 4 8 800 880 860 802 801 fffe 800 800 800 0 200 200 4200 33fe 4 208 400 9fc 3022 c042
  //   3082 902 402 20e 200 0 200 202 4204 33f8 4 100a 1412 1222 9142 7082 1342 1c22 101a 1002 2 0 100 100
  //   200 400 800 1000 2000 c3ff 2000 1000 800 400 200 100 100 0 0 1fff 8000 4000 0 47f8 4410 4410 4410
  //   47f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
  //   contents of rom_147 (hex, n*v repeats v):
  //   4200 33fe 4 8 800 880 860 802 801 fffe 800 800 800 0 200 200 4200 33fe 4 208 400 9fc 3022 c042 3082
  //   902 402 20e 200 0 200 202 4204 33f8 4 100a 1412 1222 9142 7082 1342 1c22 101a 1002 2 0 100 100 200
  //   400 800 1000 2000 c3ff 2000 1000 800 400 200 100 100 0 0 1fff 8000 4000 0 47f8 4410 4410 4410 47f8
  //   40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
  //   contents of rom_148 (hex, n*v repeats v):
  //   33fe 4 8 800 880 860 802 801 fffe 800 800 800 0 200 200 4200 33fe 4 208 400 9fc 3022 c042 3082 902
  //   402 20e 200 0 200 202 4204 33f8 4 100a 1412 1222 9142 7082 1342 1c22 101a 1002 2 0 100 100 200 400
  //   800 1000 2000 c3ff 2000 1000 800 400 200 100 100 0 0 1fff 8000 4000 0 47f8 4410 4410 4410 47f8 4000
  //   40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
  //   contents of rom_149 (hex, n*v repeats v):
  //   4 8 800 880 860 802 801 fffe 800 800 800 0 200 200 4200 33fe 4 208 400 9fc 3022 c042 3082 902 402
  //   20e 200 0 200 202 4204 33f8 4 100a 1412 1222 9142 7082 1342 1c22 101a 1002 2 0 100 100 200 400 800
  //   1000 2000 c3ff 2000 1000 800 400 200 100 100 0 0 1fff 8000 4000 0 47f8 4410 4410 4410 47f8 4000 4002
  //   40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
  //   contents of rom_150 (hex, n*v repeats v):
  //   8 800 880 860 802 801 fffe 800 800 800 0 200 200 4200 33fe 4 208 400 9fc 3022 c042 3082 902 402 20e
  //   200 0 200 202 4204 33f8 4 100a 1412 1222 9142 7082 1342 1c22 101a 1002 2 0 100 100 200 400 800 1000
  //   2000 c3ff 2000 1000 800 400 200 100 100 0 0 1fff 8000 4000 0 47f8 4410 4410 4410 47f8 4000 4002 4001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
  //   contents of rom_151 (hex, n*v repeats v):
  //   800 880 860 802 801 fffe 800 800 800 0 200 200 4200 33fe 4 208 400 9fc 3022 c042 3082 902 402 20e
  //   200 0 200 202 4204 33f8 4 100a 1412 1222 9142 7082 1342 1c22 101a 1002 2 0 100 100 200 400 800 1000
  //   2000 c3ff 2000 1000 800 400 200 100 100 0 0 1fff 8000 4000 0 47f8 4410 4410 4410 47f8 4000 4002 4001
  //   7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
  //   contents of rom_152 (hex, n*v repeats v):
  //   880 860 802 801 fffe 800 800 800 0 200 200 4200 33fe 4 208 400 9fc 3022 c042 3082 902 402 20e 200 0
  //   200 202 4204 33f8 4 100a 1412 1222 9142 7082 1342 1c22 101a 1002 2 0 100 100 200 400 800 1000 2000
  //   c3ff 2000 1000 800 400 200 100 100 0 0 1fff 8000 4000 0 47f8 4410 4410 4410 47f8 4000 4002 4001 7ffe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
  //   contents of rom_153 (hex, n*v repeats v):
  //   860 802 801 fffe 800 800 800 0 200 200 4200 33fe 4 208 400 9fc 3022 c042 3082 902 402 20e 200 0 200
  //   202 4204 33f8 4 100a 1412 1222 9142 7082 1342 1c22 101a 1002 2 0 100 100 200 400 800 1000 2000 c3ff
  //   2000 1000 800 400 200 100 100 0 0 1fff 8000 4000 0 47f8 4410 4410 4410 47f8 4000 4002 4001 7ffe 0 0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
  //   contents of rom_154 (hex, n*v repeats v):
  //   802 801 fffe 800 800 800 0 200 200 4200 33fe 4 208 400 9fc 3022 c042 3082 902 402 20e 200 0 200 202
  //   4204 33f8 4 100a 1412 1222 9142 7082 1342 1c22 101a 1002 2 0 100 100 200 400 800 1000 2000 c3ff 2000
  //   1000 800 400 200 100 100 0 0 1fff 8000 4000 0 47f8 4410 4410 4410 47f8 4000 4002 4001 7ffe 0 0 101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
  //   contents of rom_155 (hex, n*v repeats v):
  //   801 fffe 800 800 800 0 200 200 4200 33fe 4 208 400 9fc 3022 c042 3082 902 402 20e 200 0 200 202 4204
  //   33f8 4 100a 1412 1222 9142 7082 1342 1c22 101a 1002 2 0 100 100 200 400 800 1000 2000 c3ff 2000 1000
  //   800 400 200 100 100 0 0 1fff 8000 4000 0 47f8 4410 4410 4410 47f8 4000 4002 4001 7ffe 0 0 101 106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
  //   contents of rom_156 (hex, n*v repeats v):
  //   fffe 800 800 800 0 200 200 4200 33fe 4 208 400 9fc 3022 c042 3082 902 402 20e 200 0 200 202 4204
  //   33f8 4 100a 1412 1222 9142 7082 1342 1c22 101a 1002 2 0 100 100 200 400 800 1000 2000 c3ff 2000 1000
  //   800 400 200 100 100 0 0 1fff 8000 4000 0 47f8 4410 4410 4410 47f8 4000 4002 4001 7ffe 0 0 101 106
  //   7d38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
  //   contents of rom_157 (hex, n*v repeats v):
  //   800 800 800 0 200 200 4200 33fe 4 208 400 9fc 3022 c042 3082 902 402 20e 200 0 200 202 4204 33f8 4
  //   100a 1412 1222 9142 7082 1342 1c22 101a 1002 2 0 100 100 200 400 800 1000 2000 c3ff 2000 1000 800
  //   400 200 100 100 0 0 1fff 8000 4000 0 47f8 4410 4410 4410 47f8 4000 4002 4001 7ffe 0 0 101 106 7d38
  //   5504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
  //   contents of rom_158 (hex, n*v repeats v):
  //   800 800 0 200 200 4200 33fe 4 208 400 9fc 3022 c042 3082 902 402 20e 200 0 200 202 4204 33f8 4 100a
  //   1412 1222 9142 7082 1342 1c22 101a 1002 2 0 100 100 200 400 800 1000 2000 c3ff 2000 1000 800 400 200
  //   100 100 0 0 1fff 8000 4000 0 47f8 4410 4410 4410 47f8 4000 4002 4001 7ffe 0 0 101 106 7d38 5504 55f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
  //   contents of rom_159 (hex, n*v repeats v):
  //   800 0 200 200 4200 33fe 4 208 400 9fc 3022 c042 3082 902 402 20e 200 0 200 202 4204 33f8 4 100a 1412
  //   1222 9142 7082 1342 1c22 101a 1002 2 0 100 100 200 400 800 1000 2000 c3ff 2000 1000 800 400 200 100
  //   100 0 0 1fff 8000 4000 0 47f8 4410 4410 4410 47f8 4000 4002 4001 7ffe 0 0 101 106 7d38 5504 55fe 55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
  //   contents of rom_160 (hex, n*v repeats v):
  //   0 200 200 4200 33fe 4 208 400 9fc 3022 c042 3082 902 402 20e 200 0 200 202 4204 33f8 4 100a 1412
  //   1222 9142 7082 1342 1c22 101a 1002 2 0 100 100 200 400 800 1000 2000 c3ff 2000 1000 800 400 200 100
  //   100 0 0 1fff 8000 4000 0 47f8 4410 4410 4410 47f8 4000 4002 4001 7ffe 0 0 101 106 7d38 5504 55fe
  //   5522 7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
endmodule
