// Logisim project lab8_2.circ as structural Verilog: 3 circuits, main circuit main
module main (
  input  sw,
  input  rst,
  output [3:0] out_3
);

  wire and_1_out, and_2_out, clk_out, d_ff_1_q, d_ff_2_q, d_ff_3_q, d_ff_4_q, not_1_out, not_2_out,
       not_3_out, or_1_out;
  wire [3:0] adder_1_out;

  Clock clk (.out(clk_out));
  not not_1 (not_1_out, sw);
  D_Flip_Flop d_ff_1 (.clk(clk_out), .D(sw), .Q(d_ff_1_q));  // open: Qn, preset, en, reset
  D_Flip_Flop d_ff_2 (.clk(clk_out), .D(not_1_out), .Q(d_ff_2_q));  // open: Qn, preset, en, reset
  D_Flip_Flop d_ff_3 (.clk(clk_out), .D(d_ff_1_q), .Q(d_ff_3_q));  // open: Qn, preset, en, reset
  not not_2 (not_2_out, d_ff_3_q);
  not not_3 (not_3_out, d_ff_4_q);
  D_Flip_Flop d_ff_4 (.clk(clk_out), .D(d_ff_2_q), .Q(d_ff_4_q));  // open: Qn, preset, en, reset
  and and_1 (and_1_out, not_2_out, d_ff_1_q);
  and and_2 (and_2_out, not_3_out, d_ff_2_q);
  Adder #(.width(4)) adder_1 (.a(out_3), .b(4'b0001), .out(adder_1_out));  // open: cin, cout
  or or_1 (or_1_out, and_1_out, and_2_out);
  d_ff d_ff_5 (.in_1(adder_1_out), .in_2(or_1_out), .in_3(rst), .out_4(out_3));

  // Notes on the sheet:
  //   PB20000113孔浩宇
endmodule

module d_ff (
  input  [3:0] in_1,
  input  in_2,
  input  in_3,
  output [3:0] out_4
);

  D_Flip_Flop d_ff_1 (.clk(in_2), .D(in_1[0]), .Q(out_4[0]), .reset(in_3));  // open: Qn, preset, en
  D_Flip_Flop d_ff_2 (.clk(in_2), .D(in_1[1]), .Q(out_4[1]), .reset(in_3));  // open: Qn, preset, en
  D_Flip_Flop d_ff_3 (.clk(in_2), .D(in_1[2]), .Q(out_4[2]), .reset(in_3));  // open: Qn, preset, en
  D_Flip_Flop d_ff_4 (.clk(in_2), .D(in_1[3]), .Q(out_4[3]), .reset(in_3));  // open: Qn, preset, en
endmodule

module d_ff_2 (
  input  [3:0] in_1,
  input  in_2,
  input  in_3,
  output [3:0] out_4
);

  D_Flip_Flop #(.trigger("falling")) d_ff_1 (
    .clk(in_2), .D(in_1[0]), .Q(out_4[0]), .reset(in_3));  // open: Qn, preset, en
  D_Flip_Flop #(.trigger("falling")) d_ff_2 (
    .clk(in_2), .D(in_1[1]), .Q(out_4[1]), .reset(in_3));  // open: Qn, preset, en
  D_Flip_Flop #(.trigger("falling")) d_ff_3 (
    .clk(in_2), .D(in_1[2]), .Q(out_4[2]), .reset(in_3));  // open: Qn, preset, en
  D_Flip_Flop #(.trigger("falling")) d_ff_4 (
    .clk(in_2), .D(in_1[3]), .Q(out_4[3]), .reset(in_3));  // open: Qn, preset, en
endmodule
